// Logisim project Cache.circ as structural Verilog: 9 circuits, main circuit main
module main (
  input  EnableTestHalting,
  output [9:0] CorrectCounter,
  output [9:0] HitCounter,
  output [9:0] MissCounter,
  output [9:0] TestNumber,
  output [7:0] ByteRead,
  output [7:0] CorrectByteRead,
  output Halt
);

  wire and_3_out, and_4_out, and_5_out, CLK, CmdIsRead, Correct, CpuRead, CpuWrite, DidContain, HaltTesting,
       MaxItersReached, MemRead, MemWrite, not_1_out, not_2_out, not_4_out, NotDoneTesting, Ok2Count,
       or_1_out, Ready;
  wire [7:0] CpuWriteValue, MemAddress;
  wire [9:0] CpuAddress;
  wire [31:0] Line2Mem, LineFromMem;

  not not_1 (not_1_out, Ready);
  Clock clock_1 (.out(CLK));
  or or_1 (or_1_out, MaxItersReached, Ready);
  Counter #(.width(4), .max('h9)) MaxClocks (
    .load(Ready), .D(4'b0001), .count(not_1_out), .carry(MaxItersReached), .clk(CLK));  // open: Q, clr
  and and_1 (HaltTesting, EnableTestHalting, CmdIsRead, not_2_out);
  not not_2 (not_2_out, Correct);
  not not_3 (NotDoneTesting, Halt);
  Inputs inputs_1 (
    .HaltTesting(HaltTesting), .Ready(or_1_out), .CLK(CLK), .Done(Halt), .Read(CpuRead), .Write(CpuWrite),
    .Address(CpuAddress), .Value(CpuWriteValue), .TestNumber(TestNumber));
  Cache cache_1 (
    .CpuAddress(CpuAddress), .CpuRead(CpuRead), .CpuWrite(CpuWrite), .CpuWriteValue(CpuWriteValue),
    .CLK(CLK), .Ready(Ready), .isFound(DidContain), .ByteRead(ByteRead), .MemAddress(MemAddress),
    .MemRead(MemRead), .MemWrite(MemWrite), .LineFromMem(LineFromMem), .Line2Mem(Line2Mem));
  // Probe on CpuRead
  // Probe on CpuWrite
  // Probe on CpuAddress
  // Probe on CpuWriteValue
  // Probe on TestNumber
  // Probe on CorrectByteRead
  // Probe on Correct
  // Probe on Ready
  // Probe on DidContain
  // Probe on ByteRead
  // Probe on MemAddress
  // Probe on MemRead
  // Probe on MemWrite
  // Probe on HitCounter
  // Probe on LineFromMem
  // Probe on Line2Mem
  not not_4 (not_4_out, HaltTesting);
  RAM #(.dataWidth(32), .bus("separate")) ram_1 (
    .addr(MemAddress), .din(Line2Mem), .data(LineFromMem), .str(MemWrite), .clk(CLK), .ld(MemRead));  // open: sel, clr
  and and_2 (Ok2Count, Ready, not_4_out, NotDoneTesting);
  and and_3 (and_3_out, Correct, Ok2Count);
  and and_4 (and_4_out, DidContain, Ok2Count);
  and and_5 (and_5_out, MemRead, NotDoneTesting);
  Checker checker_1 (
    .TestNumber(TestNumber), .YourByteRead(ByteRead), .CmdIsRead(CmdIsRead),
    .CorrectByteRead(CorrectByteRead), .Correct(Correct));
  Counter #(.width(10), .max('h3ff)) u_CorrectCounter (
    .count(and_3_out), .Q(CorrectCounter), .clk(CLK));  // open: load, D, carry, clr
  Counter #(.width(10), .max('h3ff)) u_HitCounter (
    .count(and_4_out), .Q(HitCounter), .clk(CLK));  // open: load, D, carry, clr
  Counter #(.width(10), .max('h3ff)) u_MissCounter (
    .count(and_5_out), .Q(MissCounter), .clk(CLK));  // open: load, D, carry, clr
  // Probe on CorrectCounter
  // Probe on HitCounter
  // Probe on MissCounter

  // Other names for the same wires on the sheet: DoneTesting = Halt

  // Notes on the sheet:
  //   Your Answer Inside Here
endmodule

module Cache (
  input  [9:0] CpuAddress,
  input  CpuRead,
  input  CpuWrite,
  input  [7:0] CpuWriteValue,
  input  CLK,
  input  [31:0] LineFromMem,
  output Ready,
  output isFound,
  output [7:0] ByteRead,
  output [7:0] MemAddress,
  output MemRead,
  output MemWrite,
  output [31:0] Line2Mem
);

  wire age, contained, demultiplexer_1_out0, demultiplexer_1_out1, dirty, fsm_1_start, isdirty, newAge,
       newDirty, newTag, newValid, or_1_out, or_2_out, read_q, save, seta_contained, seta_dirty_2,
       setb_contained, setb_dirty_2, statechange_1_saveblock, valid, valida, validb, write, write_q,
       writevalue;
  wire [2:0] fsm_1_y0, state, statechange_1_y2;
  wire [6:0] seta_tag_2, setb_tag_2;
  wire [7:0] multiplexer_1_out, seta_byte, setb_byte, writetocpu;
  wire [9:0] address;
  wire [31:0] seta_block, setb_block;

  Register #(.width(1)) u_write (.D(CpuWrite), .en(save), .Q(write_q), .clk(CLK));  // open: clr
  Register #(.width(1)) read (.D(CpuRead), .en(save), .Q(read_q), .clk(CLK));  // open: clr
  Register #(.width(10)) u_address (.D(CpuAddress), .en(save), .Q(address), .clk(CLK));  // open: clr
  fsm fsm_1 (
    .x2(state[2]), .x1(state[1]), .x0(state[0]), .read(read_q), .write(write_q), .isDirty(isdirty),
    .isFound(isFound), .y2(fsm_1_y0[2]), .y1(fsm_1_y0[1]), .y0(fsm_1_y0[0]), .readOut(MemRead),
    .readWrite(MemWrite), .isReady(Ready), .ageOut(age), .saveInputs(save), .start(fsm_1_start),
    .dirtyOut(dirty), .validOut(valid));
  Demultiplexer #(.enable("false")) demultiplexer_1 (
    .out0(demultiplexer_1_out0), .out1(demultiplexer_1_out1), .in(1'b1), .sel(address[2]));
  stateChange statechange_1 (
    .x2(state[2]), .x1(state[1]), .x0(state[0]), .read(read_q), .write(write_q), .isDirty(isdirty),
    .isFound(isFound), .y2(statechange_1_y2[0]), .y1(statechange_1_y2[1]), .y0(statechange_1_y2[2]),
    .writeTo(write), .writeVal(writevalue), .dirtyNew(newDirty), .validNew(newValid), .ageNew(newAge),
    .tagNew(newTag), .saveBlock(statechange_1_saveblock));
  Register #(.width(3)) u_state (.D(statechange_1_y2), .en(1'b1), .Q(state), .clk(CLK));  // open: clr
  or or_1 (or_1_out, age, demultiplexer_1_out0);
  Register writeCPU (.D(CpuWriteValue), .en(save), .Q(writetocpu), .clk(CLK));  // open: clr
  or or_2 (or_2_out, age, demultiplexer_1_out1);
  Register #(.width(3)) state_2 (.D(fsm_1_y0), .en(1'b1), .Q(state), .clk(CLK));  // open: clr
  Register #(.width(1)) u_contained (.D(contained), .en(fsm_1_start), .Q(isFound), .clk(CLK));  // open: clr
  set seta (
    .start(or_1_out), .valid(valid), .tag(address[9:3]), .dirty(dirty), .tagNew(newTag), .ageNew(newAge),
    .validNew(newValid), .offset(address[1:0]), .saveBlock(statechange_1_saveblock), .dirtyNew(newDirty),
    .age(age), .blockMem(LineFromMem), .write(write), .writeCPU(writetocpu), .value(writevalue), .CLK(CLK),
    .valid_2(valida), .dirty_2(seta_dirty_2), .tag_2(seta_tag_2), .block(seta_block),
    .contained(seta_contained), .\byte (seta_byte));
  set setb (
    .start(or_2_out), .valid(valid), .tag(address[9:3]), .dirty(dirty), .tagNew(newTag), .ageNew(newAge),
    .validNew(newValid), .offset(address[1:0]), .saveBlock(statechange_1_saveblock), .dirtyNew(newDirty),
    .age(age), .blockMem(LineFromMem), .write(write), .writeCPU(writetocpu), .value(writevalue), .CLK(CLK),
    .valid_2(validb), .dirty_2(setb_dirty_2), .tag_2(setb_tag_2), .block(setb_block),
    .contained(setb_contained), .\byte (setb_byte));
  Multiplexer #(.width(8), .enable("false")) multiplexer_1 (
    .in0({seta_tag_2, 1'b0}), .in1({setb_tag_2, 1'b1}), .out(multiplexer_1_out), .sel(address[2]));
  Multiplexer #(.enable("false")) multiplexer_2 (
    .in0(seta_contained), .in1(setb_contained), .out(contained), .sel(address[2]));
  Multiplexer #(.width(8), .enable("false")) multiplexer_3 (
    .in0(seta_byte), .in1(setb_byte), .out(ByteRead), .sel(address[2]));
  Multiplexer #(.width(32), .enable("false")) multiplexer_4 (
    .in0(seta_block), .in1(setb_block), .out(Line2Mem), .sel(address[2]));
  Multiplexer #(.enable("false")) multiplexer_5 (
    .in0(seta_dirty_2), .in1(setb_dirty_2), .out(isdirty), .sel(address[2]));
  Multiplexer #(.width(8), .enable("false")) multiplexer_6 (
    .in0(address[9:2]), .in1(multiplexer_1_out), .out(MemAddress), .sel(MemWrite));

  // Other names for the same wires on the sheet: offset[1:0] = address[1:0]; set = address[2];
  //   tag[6:0] = address[9:3]; MemAddr[7:0] = MemAddress

  // Notes on the sheet:
  //   Address Bits = 10
  //   Line Size = 4
  //   W = 3
  //   Num Sets = 2
  //   C =4*3*2 = 24bytes
  //   Tag bits = 7
endmodule

module Inputs (
  input  HaltTesting,
  input  Ready,
  input  CLK,
  output Done,
  output Read,
  output Write,
  output [9:0] Address,
  output [7:0] Value,
  output [9:0] TestNumber
);

  wire and_1_out, not_1_out, not_2_out;

  not not_1 (not_1_out, HaltTesting);
  not not_2 (not_2_out, Done);
  Counter #(.width(10), .max('h3ff), .ongoal("stay")) u_TestNumber (
    .count(and_1_out), .Q(TestNumber), .clk(CLK));  // open: load, D, carry, clr
  and and_1 (and_1_out, not_1_out, Ready, not_2_out);
  ROM #(.addrWidth(10), .dataWidth(21)) rom_1 (
    .addr(TestNumber), .data({Done, Read, Write, Address, Value}));  // open: sel

  // Notes on the sheet:
  //   contents of rom_1 (hex, n*v repeats v):
  //   80882 83fe6 4306b 83e0e 43701 42275 8280f 80304 41bd8 84371 43f77 41d70 4250b 44733 8253d 440d8
  //   82691 440c9 83d7c 43558 446bf 83837 842c9 43e0f 4059d 41556 80166 833b0 43a89 83142 8361c 42e66
  //   43eb6 42c00 43a0e 8165c 84682 8092a 83907 41f89 817b0 40855 82056 425e8 43ff2 8039f 42bd7 82137
  //   4416b 40273 8324a 814e4 44570 41c0f 429da 82640 8069c 8099e 414d5 41004 81beb 84113 419b1 81add
  //   83f35 425ff 829cd 40250 82945 4366d 40cc2 444f8 80814 81156 8446d 42a82 42bae 82578 41135 405d0
  //   8304b 82b3a 40972 822ba 4443a 42337 82506 80bd3 80560 83552 83955 81434 43096 43da1 81aa2 80305
  //   428e6 428cc 808a2 40e80 845f0 4215d 82765 82e29 40be5 82b74 42715 417a2 41fab 8452f 81c0a 83325
  //   44624 80205 42dfc 41333 40958 81348 42736 41069 84510 44669 826dd 8067e 408e4 44680 444e8 832ad
  //   821f8 83509 82d46 81184 432cd 80b77 4005a 440e0 81ea0 43d73 42b8c 80624 41468 42699 415ed 80fc1 0
  //   100000
endmodule

module Checker (
  input  [9:0] TestNumber,
  input  [7:0] YourByteRead,
  output CmdIsRead,
  output [7:0] CorrectByteRead,
  output Correct
);

  wire comparator_1_eq;
  wire [9:0] subtractor_1_out;

  // Probe on TestNumber
  Subtractor #(.width(10)) subtractor_1 (.a(TestNumber), .b(10'h1), .out(subtractor_1_out));  // open: bin, bout
  ROM #(.addrWidth(10), .dataWidth(9)) rom_1 (
    .addr(subtractor_1_out), .data({CmdIsRead, CorrectByteRead}));  // open: sel
  Comparator #(.mode("unsigned")) comparator_1 (
    .a(YourByteRead), .b(CorrectByteRead), .eq(comparator_1_eq));  // open: gt, lt
  and and_1 (Correct, comparator_1_eq, CmdIsRead);

  // Other names for the same wires on the sheet: Test_Number[9:0] = TestNumber

  // Notes on the sheet:
  //   Read Solutions
  //   contents of rom_1 (hex, n*v repeats v):
  //   1a3 1dc 6b 125 1 75 1dc 1c3 d8 1ab 77 70 b 33 10b d8 1c3 c9 174 58 bf 153 199 f 9d 56 1bb 13b 89 16c
  //   180 66 b6 0 e 107 1bf 1d8 167 89 118 55 1a2 e8 f2 1c3 d7 142 6b 73 1ab 18c 70 f da 1c3 14c 1d8 d5 4
  //   1d8 16b b1 1f4 1f2 ff 1da 50 1da 6d c2 f8 155 1c6 1f8 82 ae 1ff 35 d0 16b 1ae 72 175 3a 37 1ff 173
  //   1d0 158 167 1d5 96 a1 1f4 1c3 e6 cc 155 80 170 5d 1e6 166 e5 1ae 15 a2 ab 170 10f 13b 24 150 fc 33
  //   58 133 36 69 170 69 1c3 14c e4 80 e8 1ab 15d 158 1fc 135 cd 1e5 5a e0 104 73 8c 14c 68 99 ed 1a6
endmodule

module fsm (
  input  x2,
  input  x1,
  input  x0,
  input  read,
  input  write,
  input  isDirty,
  input  isFound,
  output y2,
  output y1,
  output y0,
  output readOut,
  output readWrite,
  output isReady,
  output ageOut,
  output saveInputs,
  output start,
  output dirtyOut,
  output validOut
);

  wire nand_1_out, nand_2_out, nand_3_out, nand_4_out, nand_5_out, nand_6_out, nand_7_out, nand_8_out,
       nand_9_out, nand_10_out, nand_11_out, nand_12_out, nand_13_out, nand_14_out, nand_15_out, nand_16_out,
       nand_17_out, nand_18_out, nand_19_out, nand_20_out, nand_21_out, nand_22_out, nand_23_out,
       nand_24_out, nand_25_out, nand_26_out, nand_27_out, nand_28_out, nand_29_out, nand_30_out,
       nand_31_out, nand_32_out, nand_33_out, nand_34_out, nand_35_out, nand_36_out, nand_37_out,
       nand_38_out, nand_39_out, nand_40_out, nand_41_out, nand_42_out, nand_43_out, nand_44_out,
       nand_45_out, nand_46_out, nand_47_out, nand_48_out, nand_49_out, nand_50_out, nand_51_out,
       nand_52_out, nand_53_out, nand_54_out, nand_55_out, nand_56_out, nand_57_out, nand_58_out,
       nand_59_out, nand_60_out, nand_61_out, nand_62_out, nand_63_out, nand_64_out, nand_65_out,
       nand_66_out, nand_67_out, nand_68_out, nand_69_out, nand_70_out, nand_71_out, nand_72_out,
       nand_73_out, nand_74_out, nand_75_out, nand_76_out, nand_77_out, nand_78_out, nand_79_out,
       nand_80_out, nand_81_out, nand_82_out, nand_83_out, nand_84_out, nand_85_out, nand_86_out,
       nand_87_out, nand_88_out, nand_89_out, nand_90_out, nand_91_out, nand_92_out, nand_93_out,
       nand_94_out, nand_95_out, nand_96_out, nand_97_out, nand_98_out, nand_99_out, nand_100_out,
       nand_101_out, nand_102_out, nand_103_out, nand_104_out, nand_105_out, nand_106_out, nand_107_out,
       nand_108_out, nand_109_out, nand_110_out, nand_111_out, nand_112_out, nand_113_out, nand_114_out,
       nand_115_out, nand_116_out, nand_117_out, nand_118_out, nand_119_out, nand_120_out, nand_121_out,
       nand_122_out, nand_123_out, nand_124_out, nand_125_out, nand_126_out, nand_127_out, nand_128_out,
       nand_129_out, nand_130_out, nand_131_out, nand_132_out, nand_133_out, nand_134_out, nand_135_out,
       nand_136_out, nand_137_out, nand_138_out, nand_139_out, nand_140_out, nand_141_out, nand_142_out,
       nand_143_out, nand_144_out, nand_145_out, nand_146_out, nand_147_out, nand_148_out, nand_149_out,
       nand_150_out, nand_151_out, nand_152_out, nand_153_out, nand_154_out, nand_157_out, nand_158_out,
       nand_159_out, nand_162_out, nand_163_out, nand_164_out, nand_165_out, nand_166_out, nand_167_out,
       nand_168_out, nand_169_out, nand_170_out, nand_171_out, nand_172_out, nand_173_out, nand_174_out,
       nand_175_out, nand_176_out, nand_177_out, nand_178_out, nand_179_out, nand_180_out, nand_181_out,
       nand_183_out, nand_184_out, nand_190_out, nand_191_out;

  nand nand_1 (nand_1_out, x2, x2);
  nand nand_2 (nand_2_out, x1, x1);
  nand nand_3 (nand_3_out, read, read);
  nand nand_4 (nand_4_out, x1, x1);
  nand nand_5 (nand_5_out, write, write);
  nand nand_6 (nand_6_out, read, read);
  nand nand_7 (nand_7_out, write, write);
  nand nand_8 (nand_8_out, isFound, isFound);
  nand nand_9 (nand_9_out, x2, x2);
  nand nand_10 (nand_10_out, x2, x2);
  nand nand_11 (nand_11_out, x2, x2);
  nand nand_12 (nand_12_out, x2, x2);
  nand nand_13 (nand_13_out, x1, x1);
  nand nand_14 (nand_14_out, x2, x2);
  nand nand_15 (nand_15_out, x1, x1);
  nand nand_16 (nand_16_out, x2, x2);
  nand nand_17 (nand_17_out, x1, x1);
  nand nand_18 (nand_18_out, x2, x2);
  nand nand_19 (nand_19_out, x1, x1);
  nand nand_20 (nand_20_out, x2, x2);
  nand nand_21 (nand_21_out, x1, x1);
  nand nand_22 (nand_22_out, x2, x2);
  nand nand_23 (nand_23_out, x1, x1);
  nand nand_24 (nand_24_out, read, read);
  nand nand_25 (nand_25_out, x2, x2);
  nand nand_26 (nand_26_out, x2, x2);
  nand nand_27 (nand_27_out, x0, x0);
  nand nand_28 (nand_28_out, read, read);
  nand nand_29 (nand_29_out, x0, x0);
  nand nand_30 (nand_30_out, read, read);
  nand nand_31 (nand_31_out, x2, x2);
  nand nand_32 (nand_32_out, nand_1_out, x1);
  nand nand_33 (nand_33_out, nand_2_out, x0);
  nand nand_34 (nand_34_out, nand_3_out, write);
  nand nand_35 (nand_35_out, nand_4_out, x0);
  nand nand_36 (nand_36_out, read, nand_5_out);
  nand nand_37 (nand_37_out, nand_6_out, nand_7_out);
  nand nand_38 (nand_38_out, x1, nand_8_out);
  nand nand_39 (nand_39_out, nand_9_out, x1);
  nand nand_40 (nand_40_out, nand_10_out, x1);
  nand nand_41 (nand_41_out, nand_11_out, x1);
  nand nand_42 (nand_42_out, nand_12_out, nand_13_out);
  nand nand_43 (nand_43_out, nand_14_out, nand_15_out);
  nand nand_44 (nand_44_out, nand_16_out, nand_17_out);
  nand nand_45 (nand_45_out, nand_18_out, nand_19_out);
  nand nand_46 (nand_46_out, nand_20_out, nand_21_out);
  nand nand_47 (nand_47_out, nand_22_out, nand_23_out);
  nand nand_48 (nand_48_out, nand_24_out, write);
  nand nand_49 (nand_49_out, nand_25_out, x1);
  nand nand_50 (nand_50_out, nand_26_out, x1);
  nand nand_51 (nand_51_out, x2, x1);
  nand nand_52 (nand_52_out, nand_27_out, nand_28_out);
  nand nand_53 (nand_53_out, x2, x1);
  nand nand_54 (nand_54_out, nand_29_out, nand_30_out);
  nand nand_55 (nand_55_out, nand_31_out, x1);
  nand nand_56 (nand_56_out, nand_32_out, nand_32_out);
  nand nand_57 (nand_57_out, x1, x1);
  nand nand_58 (nand_58_out, x0, x0);
  nand nand_59 (nand_59_out, nand_33_out, nand_33_out);
  nand nand_60 (nand_60_out, nand_34_out, nand_34_out);
  nand nand_61 (nand_61_out, nand_35_out, nand_35_out);
  nand nand_62 (nand_62_out, nand_36_out, nand_36_out);
  nand nand_63 (nand_63_out, x2, x2);
  nand nand_64 (nand_64_out, x0, x0);
  nand nand_65 (nand_65_out, x2, x2);
  nand nand_66 (nand_66_out, x0, nand_37_out);
  nand nand_67 (nand_67_out, nand_38_out, nand_38_out);
  nand nand_68 (nand_68_out, isDirty, isDirty);
  nand nand_69 (nand_69_out, nand_39_out, nand_39_out);
  nand nand_70 (nand_70_out, isFound, isFound);
  nand nand_71 (nand_71_out, isDirty, isDirty);
  nand nand_72 (nand_72_out, x1, x1);
  nand nand_73 (nand_73_out, nand_40_out, nand_40_out);
  nand nand_74 (nand_74_out, isFound, isFound);
  nand nand_75 (nand_75_out, nand_41_out, nand_41_out);
  nand nand_76 (nand_76_out, isFound, isFound);
  nand nand_77 (nand_77_out, nand_42_out, nand_42_out);
  nand nand_78 (nand_78_out, nand_43_out, nand_43_out);
  nand nand_79 (nand_79_out, nand_44_out, nand_44_out);
  nand nand_80 (nand_80_out, x0, x0);
  nand nand_81 (nand_81_out, nand_45_out, nand_45_out);
  nand nand_82 (nand_82_out, x0, x0);
  nand nand_83 (nand_83_out, nand_46_out, nand_46_out);
  nand nand_84 (nand_84_out, x0, x0);
  nand nand_85 (nand_85_out, nand_47_out, nand_47_out);
  nand nand_86 (nand_86_out, nand_48_out, nand_48_out);
  nand nand_87 (nand_87_out, x2, x2);
  nand nand_88 (nand_88_out, x1, x1);
  nand nand_89 (nand_89_out, write, write);
  nand nand_90 (nand_90_out, nand_49_out, nand_49_out);
  nand nand_91 (nand_91_out, x0, x0);
  nand nand_92 (nand_92_out, nand_50_out, nand_50_out);
  nand nand_93 (nand_93_out, x0, x0);
  nand nand_94 (nand_94_out, nand_51_out, nand_51_out);
  nand nand_95 (nand_95_out, nand_52_out, nand_52_out);
  nand nand_96 (nand_96_out, nand_53_out, nand_53_out);
  nand nand_97 (nand_97_out, nand_54_out, nand_54_out);
  nand nand_98 (nand_98_out, nand_55_out, nand_55_out);
  nand nand_99 (nand_99_out, isFound, isFound);
  nand nand_100 (nand_100_out, isDirty, isDirty);
  nand nand_101 (nand_101_out, x1, x1);
  nand nand_102 (nand_102_out, nand_56_out, x0);
  nand nand_103 (nand_103_out, x2, nand_57_out);
  nand nand_104 (nand_104_out, x2, nand_58_out);
  nand nand_105 (nand_105_out, nand_59_out, nand_60_out);
  nand nand_106 (nand_106_out, nand_61_out, nand_62_out);
  nand nand_107 (nand_107_out, nand_63_out, x1);
  nand nand_108 (nand_108_out, x1, nand_64_out);
  nand nand_109 (nand_109_out, nand_65_out, x1);
  nand nand_110 (nand_110_out, nand_66_out, nand_66_out);
  nand nand_111 (nand_111_out, read, write);
  nand nand_112 (nand_112_out, nand_67_out, nand_68_out);
  nand nand_113 (nand_113_out, x2, x1);
  nand nand_114 (nand_114_out, nand_69_out, x0);
  nand nand_115 (nand_115_out, nand_70_out, nand_71_out);
  nand nand_116 (nand_116_out, x2, nand_72_out);
  nand nand_117 (nand_117_out, nand_73_out, x0);
  nand nand_118 (nand_118_out, nand_74_out, isDirty);
  nand nand_119 (nand_119_out, nand_75_out, x0);
  nand nand_120 (nand_120_out, nand_76_out, isDirty);
  nand nand_121 (nand_121_out, nand_77_out, x0);
  nand nand_122 (nand_122_out, nand_78_out, x0);
  nand nand_123 (nand_123_out, nand_79_out, nand_80_out);
  nand nand_124 (nand_124_out, nand_81_out, nand_82_out);
  nand nand_125 (nand_125_out, nand_83_out, nand_84_out);
  nand nand_126 (nand_126_out, nand_85_out, nand_86_out);
  nand nand_127 (nand_127_out, nand_87_out, nand_88_out);
  nand nand_128 (nand_128_out, read, nand_89_out);
  nand nand_129 (nand_129_out, nand_90_out, nand_91_out);
  nand nand_130 (nand_130_out, nand_92_out, nand_93_out);
  nand nand_131 (nand_131_out, nand_94_out, nand_95_out);
  nand nand_132 (nand_132_out, nand_96_out, nand_97_out);
  nand nand_133 (nand_133_out, nand_98_out, x0);
  nand nand_134 (nand_134_out, nand_99_out, nand_100_out);
  nand nand_135 (nand_135_out, x2, nand_101_out);
  nand nand_136 (nand_136_out, nand_102_out, nand_103_out);
  nand nand_137 (nand_137_out, nand_104_out, nand_104_out);
  nand nand_138 (nand_138_out, read, read);
  nand nand_139 (nand_139_out, nand_105_out, nand_106_out);
  nand nand_140 (nand_140_out, nand_107_out, nand_107_out);
  nand nand_141 (nand_141_out, x0, x0);
  nand nand_142 (nand_142_out, nand_108_out, nand_108_out);
  nand nand_143 (nand_143_out, read, read);
  nand nand_144 (nand_144_out, nand_109_out, nand_109_out);
  nand nand_145 (nand_145_out, nand_110_out, nand_111_out);
  nand nand_146 (nand_146_out, nand_112_out, nand_113_out);
  nand nand_147 (nand_147_out, nand_114_out, nand_114_out);
  nand nand_148 (nand_148_out, nand_115_out, nand_115_out);
  nand nand_149 (nand_149_out, nand_116_out, nand_116_out);
  nand nand_150 (nand_150_out, x0, x0);
  nand nand_151 (nand_151_out, nand_117_out, nand_117_out);
  nand nand_152 (nand_152_out, nand_118_out, nand_118_out);
  nand nand_153 (nand_153_out, nand_119_out, nand_119_out);
  nand nand_154 (nand_154_out, nand_120_out, nand_120_out);
  nand nand_155 (isReady, nand_121_out, nand_122_out);
  nand nand_156 (ageOut, nand_123_out, nand_124_out);
  nand nand_157 (nand_157_out, nand_125_out, nand_126_out);
  nand nand_158 (nand_158_out, nand_127_out, nand_127_out);
  nand nand_159 (nand_159_out, nand_128_out, nand_128_out);
  nand nand_160 (start, nand_129_out, nand_130_out);
  nand nand_161 (dirtyOut, nand_131_out, nand_132_out);
  nand nand_162 (nand_162_out, nand_133_out, nand_133_out);
  nand nand_163 (nand_163_out, nand_134_out, nand_134_out);
  nand nand_164 (nand_164_out, nand_135_out, nand_135_out);
  nand nand_165 (nand_165_out, x0, x0);
  nand nand_166 (nand_166_out, nand_136_out, nand_136_out);
  nand nand_167 (nand_167_out, nand_137_out, nand_138_out);
  nand nand_168 (nand_168_out, nand_139_out, nand_139_out);
  nand nand_169 (nand_169_out, nand_140_out, nand_141_out);
  nand nand_170 (nand_170_out, nand_142_out, nand_143_out);
  nand nand_171 (nand_171_out, nand_144_out, isFound);
  nand nand_172 (nand_172_out, nand_145_out, nand_145_out);
  nand nand_173 (nand_173_out, nand_146_out, nand_146_out);
  nand nand_174 (nand_174_out, nand_147_out, nand_148_out);
  nand nand_175 (nand_175_out, nand_149_out, nand_150_out);
  nand nand_176 (nand_176_out, nand_151_out, nand_152_out);
  nand nand_177 (nand_177_out, nand_153_out, nand_154_out);
  nand nand_178 (nand_178_out, nand_157_out, nand_157_out);
  nand nand_179 (nand_179_out, nand_158_out, nand_159_out);
  nand nand_180 (nand_180_out, nand_162_out, nand_163_out);
  nand nand_181 (nand_181_out, nand_164_out, nand_165_out);
  nand nand_182 (y2, nand_166_out, nand_167_out);
  nand nand_183 (nand_183_out, nand_168_out, nand_169_out);
  nand nand_184 (nand_184_out, nand_170_out, nand_171_out);
  nand nand_185 (y0, nand_172_out, nand_173_out);
  nand nand_186 (readOut, nand_174_out, nand_175_out);
  nand nand_187 (readWrite, nand_176_out, nand_177_out);
  nand nand_188 (saveInputs, nand_178_out, nand_179_out);
  nand nand_189 (validOut, nand_180_out, nand_181_out);
  nand nand_190 (nand_190_out, nand_183_out, nand_183_out);
  nand nand_191 (nand_191_out, nand_184_out, nand_184_out);
  nand nand_192 (y1, nand_190_out, nand_191_out);
endmodule

module age (
  input  [1:0] agea,
  input  [1:0] ageb,
  input  [1:0] agec,
  input  [1:0] i,
  output [1:0] age1,
  output [1:0] age2,
  output [1:0] age3
);

  wire [1:0] adder_1_out, adder_2_out, adder_3_out, multiplexer_1_out;
  wire [2:0] comparator_1_gt, comparator_2_gt, comparator_3_gt;

  Multiplexer #(.select(2), .width(2), .enable("false")) multiplexer_1 (
    .in0(agea), .in1(ageb), .in2(agec), .out(multiplexer_1_out), .sel(i));  // open: in3
  Adder #(.width(2)) adder_1 (.a(agec), .b(2'b01), .out(adder_1_out));  // open: cin, cout
  Adder #(.width(2)) adder_2 (.a(agea), .b(2'b01), .out(adder_2_out));  // open: cin, cout
  Comparator #(.width(2), .mode("unsigned")) comparator_1 (
    .a(ageb), .b(multiplexer_1_out), .gt(comparator_1_gt[0]), .eq(comparator_1_gt[1]), .lt(comparator_1_gt[2]));
  Adder #(.width(2)) adder_3 (.a(ageb), .b(2'b01), .out(adder_3_out));  // open: cin, cout
  Comparator #(.width(2), .mode("unsigned")) comparator_2 (
    .a(agec), .b(multiplexer_1_out), .gt(comparator_2_gt[0]), .eq(comparator_2_gt[1]), .lt(comparator_2_gt[2]));
  Multiplexer #(.select(3), .width(2), .enable("false")) multiplexer_2 (
    .in1(agec), .in2(2'b00), .in4(adder_1_out), .out(age3), .sel(comparator_2_gt));  // open: in0, in3, in5, in6, in7
  Comparator #(.width(2), .mode("unsigned")) comparator_3 (
    .a(agea), .b(multiplexer_1_out), .gt(comparator_3_gt[0]), .eq(comparator_3_gt[1]), .lt(comparator_3_gt[2]));
  Multiplexer #(.select(3), .width(2), .enable("false")) multiplexer_3 (
    .in1(agea), .in2(2'b00), .in4(adder_2_out), .out(age1), .sel(comparator_3_gt));  // open: in0, in3, in5, in6, in7
  Multiplexer #(.select(3), .width(2), .enable("false")) multiplexer_4 (
    .in1(ageb), .in2(2'b00), .in4(adder_3_out), .out(age2), .sel(comparator_1_gt));  // open: in0, in3, in5, in6, in7
endmodule

module block (
  input  start,
  input  ageNew,
  input  [6:0] tag,
  input  valid,
  input  dirty,
  input  tagNew,
  input  [1:0] age,
  input  validNew,
  input  write,
  input  dirtyNew,
  input  [31:0] blockMem,
  input  [1:0] offset,
  input  wval,
  input  [7:0] writeCPU,
  input  CLK,
  output [1:0] age_2,
  output [6:0] tag_2,
  output isValid,
  output [31:0] block,
  output isDirty,
  output [7:0] \byte 
);

  wire and_1_out, and_3_out, and_4_out, and_5_out, and_6_out, demultiplexer_1_out0, demultiplexer_1_out1,
       demultiplexer_1_out2, demultiplexer_1_out3, or_1_out, or_2_out, or_3_out, or_4_out, Write_t;
  wire [7:0] a, b, c, d;

  and and_1 (and_1_out, start, wval);
  and and_2 (Write_t, write, start);
  Demultiplexer #(.select(2), .enable("false")) demultiplexer_1 (
    .out0(demultiplexer_1_out0), .out1(demultiplexer_1_out1), .out2(demultiplexer_1_out2),
    .out3(demultiplexer_1_out3), .in(and_1_out), .sel(offset));
  or or_1 (or_1_out, Write_t, demultiplexer_1_out1);
  or or_2 (or_2_out, Write_t, demultiplexer_1_out0);
  Register register_1 (.D(b), .en(or_1_out), .Q(block[15:8]), .clk(CLK));  // open: clr
  Register register_2 (.D(a), .en(or_2_out), .Q(block[7:0]), .clk(CLK));  // open: clr
  or or_3 (or_3_out, Write_t, demultiplexer_1_out3);
  Multiplexer #(.width(8), .enable("false")) multiplexer_1 (.in0(blockMem[7:0]), .in1(writeCPU), .out(a), .sel(wval));
  Multiplexer #(.width(8), .enable("false")) multiplexer_2 (.in0(blockMem[15:8]), .in1(writeCPU), .out(b), .sel(wval));
  or or_4 (or_4_out, Write_t, demultiplexer_1_out2);
  Register register_3 (.D(d), .en(or_3_out), .Q(block[31:24]), .clk(CLK));  // open: clr
  Register register_4 (.D(c), .en(or_4_out), .Q(block[23:16]), .clk(CLK));  // open: clr
  Multiplexer #(.width(8), .enable("false")) multiplexer_3 (.in0(blockMem[23:16]), .in1(writeCPU), .out(c), .sel(wval));
  Multiplexer #(.width(8), .enable("false")) multiplexer_4 (.in0(blockMem[31:24]), .in1(writeCPU), .out(d), .sel(wval));
  and and_3 (and_3_out, start, tagNew);
  and and_4 (and_4_out, start, ageNew);
  and and_5 (and_5_out, start, validNew);
  Register #(.width(7)) u_tag (.D(tag), .en(and_3_out), .Q(tag_2), .clk(CLK));  // open: clr
  and and_6 (and_6_out, start, dirtyNew);
  Register #(.width(1)) u_valid (.D(valid), .en(and_5_out), .Q(isValid), .clk(CLK));  // open: clr
  Register #(.width(2)) u_age (.D(age), .en(and_4_out), .Q(age_2), .clk(CLK));  // open: clr
  Register #(.width(1)) u_dirty (.D(dirty), .en(and_6_out), .Q(isDirty), .clk(CLK));  // open: clr
  Multiplexer #(.select(2), .width(8), .enable("false")) multiplexer_5 (
    .in0(block[7:0]), .in1(block[15:8]), .in2(block[23:16]), .in3(block[31:24]), .out(\byte ), .sel(offset));

  // Other names for the same wires on the sheet: byte0Out[7:0] = block[7:0]; byte1Out[7:0] = block[15:8];
  //   byte2Out[7:0] = block[23:16]; byte3Out[7:0] = block[31:24]; byte0[7:0] = blockMem[7:0];
  //   byte1[7:0] = blockMem[15:8]; byte2[7:0] = blockMem[23:16]; byte3[7:0] = blockMem[31:24]
endmodule

module set (
  input  start,
  input  valid,
  input  [6:0] tag,
  input  dirty,
  input  tagNew,
  input  ageNew,
  input  validNew,
  input  [1:0] offset,
  input  saveBlock,
  input  dirtyNew,
  input  age,
  input  [31:0] blockMem,
  input  write,
  input  [7:0] writeCPU,
  input  value,
  input  CLK,
  output valid_2,
  output dirty_2,
  output [6:0] tag_2,
  output [31:0] block,
  output contained,
  output [7:0] \byte 
);

  wire and_1_out, and_2_out, and_3_out, and_4_out, and_5_out, blocka_isdirty, blockb_isdirty, blockc_isdirty,
       comparator_1_eq, comparator_2_eq, comparator_3_eq, comparator_4_eq, comparator_5_eq, comparator_6_eq,
       dirtya, dirtyb, dirtyc, not_1_out, not_2_out, not_3_out, saveLine, taga, tagb, tagc, vala, valb, valc,
       valid1, valid2, valid3, valida, validb, validc, writea, writeb, writec;
  wire [1:0] age_1_age1, age_1_age2, age_1_age3, agea, ageb, agec, ageNewa, ageNewb, ageNewc, block_t,
       multiplexer_1_out, multiplexer_2_out, multiplexer_3_out, multiplexer_4_out, multiplexer_5_out,
       multiplexer_6_out;
  wire [6:0] tag1, tag2, tag3;
  wire [7:0] bytea, byteb, bytec;
  wire [31:0] blocka, blockb, blockc;

  Demultiplexer #(.select(2), .enable("false")) demultiplexer_1 (
    .out0(valida), .out1(validb), .out2(validc), .in(validNew), .sel(block_t));  // open: out3
  Demultiplexer #(.select(2), .enable("false")) demultiplexer_2 (
    .out0(taga), .out1(tagb), .out2(tagc), .in(tagNew), .sel(block_t));  // open: out3
  Demultiplexer #(.select(2), .enable("false")) demultiplexer_3 (
    .out0(dirtya), .out1(dirtyb), .out2(dirtyc), .in(dirtyNew), .sel(block_t));  // open: out3
  Demultiplexer #(.select(2), .enable("false")) demultiplexer_4 (
    .out0(writea), .out1(writeb), .out2(writec), .in(write), .sel(block_t));  // open: out3
  Demultiplexer #(.select(2), .enable("false")) demultiplexer_5 (
    .out0(vala), .out1(valb), .out2(valc), .in(value), .sel(block_t));  // open: out3
  Comparator #(.width(7), .mode("unsigned")) comparator_1 (.a(tag), .b(tag2), .eq(comparator_1_eq));  // open: gt, lt
  Comparator #(.width(7), .mode("unsigned")) comparator_2 (.a(tag), .b(tag3), .eq(comparator_2_eq));  // open: gt, lt
  Comparator #(.width(2), .mode("unsigned")) comparator_3 (.a(ageb), .b(2'b10), .eq(comparator_3_eq));  // open: gt, lt
  Comparator #(.width(2), .mode("unsigned")) comparator_4 (.a(agec), .b(2'b10), .eq(comparator_4_eq));  // open: gt, lt
  and and_1 (and_1_out, comparator_1_eq, valid2);
  and and_2 (and_2_out, comparator_2_eq, valid3);
  Multiplexer #(.width(2), .enable("false")) multiplexer_1 (
    .in0(2'b10), .in1(2'b10), .out(multiplexer_1_out), .sel(comparator_4_eq));
  Comparator #(.width(7), .mode("unsigned")) comparator_5 (.a(tag), .b(tag1), .eq(comparator_5_eq));  // open: gt, lt
  not not_1 (not_1_out, and_1_out);
  not not_2 (not_2_out, and_2_out);
  Comparator #(.width(2), .mode("unsigned")) comparator_6 (.a(agea), .b(2'b10), .eq(comparator_6_eq));  // open: gt, lt
  Multiplexer #(.width(2), .enable("false")) multiplexer_2 (
    .in0(multiplexer_1_out), .in1(2'b01), .out(multiplexer_2_out), .sel(comparator_3_eq));
  and and_3 (and_3_out, comparator_5_eq, valid1);
  Multiplexer #(.width(2), .enable("false")) multiplexer_3 (
    .in0(multiplexer_2_out), .in1(2'b00), .out(multiplexer_3_out), .sel(comparator_6_eq));
  Multiplexer #(.width(2), .enable("false")) multiplexer_4 (
    .in0(multiplexer_3_out), .in1(2'b10), .out(multiplexer_4_out), .sel(and_2_out));
  not not_3 (not_3_out, and_3_out);
  Multiplexer #(.width(2), .enable("false")) multiplexer_5 (
    .in0(multiplexer_4_out), .in1(2'b01), .out(multiplexer_5_out), .sel(and_1_out));
  Multiplexer #(.width(2), .enable("false")) multiplexer_6 (
    .in0(multiplexer_5_out), .in1(2'b00), .out(multiplexer_6_out), .sel(and_3_out));
  and and_4 (and_4_out, start, saveLine);
  not not_4 (contained, and_5_out);
  and and_5 (and_5_out, not_3_out, not_1_out, not_2_out);
  Register #(.width(2)) index (.D(multiplexer_6_out), .en(and_4_out), .Q(block_t), .clk(CLK));  // open: clr
  age age_1 (
    .agea(agea), .ageb(ageb), .agec(agec), .i(block_t), .age1(age_1_age1), .age2(age_1_age2),
    .age3(age_1_age3));
  Multiplexer #(.width(2), .enable("false")) multiplexer_7 (.in0(age_1_age3), .in1(2'b10), .out(ageNewc), .sel(age));
  Multiplexer #(.width(2), .enable("false")) multiplexer_8 (.in0(age_1_age1), .in1(2'b00), .out(ageNewa), .sel(age));
  Multiplexer #(.width(2), .enable("false")) multiplexer_9 (.in0(age_1_age2), .in1(2'b01), .out(ageNewb), .sel(age));
  block u_blocka (
    .start(start), .ageNew(ageNew), .tag(tag), .valid(valid), .dirty(dirty), .tagNew(taga), .age(ageNewa),
    .validNew(valida), .write(writea), .dirtyNew(dirtya), .blockMem(blockMem), .offset(offset), .wval(vala),
    .writeCPU(writeCPU), .CLK(CLK), .age_2(agea), .tag_2(tag1), .isValid(valid1), .block(blocka),
    .isDirty(blocka_isdirty), .\byte (bytea));
  block u_blockb (
    .start(start), .ageNew(ageNew), .tag(tag), .valid(valid), .dirty(dirty), .tagNew(tagb), .age(ageNewb),
    .validNew(validb), .write(writeb), .dirtyNew(dirtyb), .blockMem(blockMem), .offset(offset), .wval(valb),
    .writeCPU(writeCPU), .CLK(CLK), .age_2(ageb), .tag_2(tag2), .isValid(valid2), .block(blockb),
    .isDirty(blockb_isdirty), .\byte (byteb));
  block u_blockc (
    .start(start), .ageNew(ageNew), .tag(tag), .valid(valid), .dirty(dirty), .tagNew(tagc), .age(ageNewc),
    .validNew(validc), .write(writec), .dirtyNew(dirtyc), .blockMem(blockMem), .offset(offset), .wval(valc),
    .writeCPU(writeCPU), .CLK(CLK), .age_2(agec), .tag_2(tag3), .isValid(valid3), .block(blockc),
    .isDirty(blockc_isdirty), .\byte (bytec));
  Multiplexer #(.select(2), .enable("false")) multiplexer_10 (
    .in0(blocka_isdirty), .in1(blockb_isdirty), .in2(blockc_isdirty), .out(dirty_2), .sel(block_t));  // open: in3
  Multiplexer #(.select(2), .width(7), .enable("false")) multiplexer_11 (
    .in0(tag1), .in1(tag2), .in2(tag3), .out(tag_2), .sel(block_t));  // open: in3
  Multiplexer #(.select(2), .width(32), .enable("false")) multiplexer_12 (
    .in0(blocka), .in1(blockb), .in2(blockc), .out(block), .sel(block_t));  // open: in3
  Multiplexer #(.select(2), .enable("false")) multiplexer_13 (
    .in0(valid1), .in1(valid2), .in2(valid3), .out(valid_2), .sel(block_t));  // open: in3
  Multiplexer #(.select(2), .width(8), .enable("false")) multiplexer_14 (
    .in0(bytea), .in1(byteb), .in2(bytec), .out(\byte ), .sel(block_t));  // open: in3
endmodule

module stateChange (
  input  x2,
  input  x1,
  input  x0,
  input  read,
  input  write,
  input  isDirty,
  input  isFound,
  output y2,
  output y1,
  output y0,
  output writeTo,
  output writeVal,
  output dirtyNew,
  output validNew,
  output ageNew,
  output tagNew,
  output saveBlock
);

  wire nand_1_out, nand_2_out, nand_3_out, nand_4_out, nand_5_out, nand_6_out, nand_7_out, nand_8_out,
       nand_9_out, nand_10_out, nand_11_out, nand_12_out, nand_13_out, nand_14_out, nand_15_out, nand_16_out,
       nand_17_out, nand_18_out, nand_19_out, nand_20_out, nand_21_out, nand_22_out, nand_23_out,
       nand_24_out, nand_25_out, nand_26_out, nand_27_out, nand_28_out, nand_29_out, nand_30_out,
       nand_31_out, nand_32_out, nand_33_out, nand_34_out, nand_35_out, nand_36_out, nand_37_out,
       nand_38_out, nand_39_out, nand_40_out, nand_41_out, nand_42_out, nand_43_out, nand_44_out,
       nand_45_out, nand_46_out, nand_47_out, nand_48_out, nand_49_out, nand_50_out, nand_51_out,
       nand_52_out, nand_53_out, nand_54_out, nand_55_out, nand_56_out, nand_57_out, nand_58_out,
       nand_59_out, nand_60_out, nand_61_out, nand_62_out, nand_63_out, nand_64_out, nand_65_out,
       nand_66_out, nand_67_out, nand_68_out, nand_69_out, nand_70_out, nand_71_out, nand_72_out,
       nand_73_out, nand_74_out, nand_75_out, nand_76_out, nand_77_out, nand_78_out, nand_79_out,
       nand_80_out, nand_81_out, nand_82_out, nand_83_out, nand_84_out, nand_85_out, nand_86_out,
       nand_87_out, nand_88_out, nand_89_out, nand_90_out, nand_91_out, nand_92_out, nand_93_out,
       nand_94_out, nand_95_out, nand_96_out, nand_97_out, nand_98_out, nand_99_out, nand_100_out,
       nand_101_out, nand_102_out, nand_103_out, nand_104_out, nand_105_out, nand_106_out, nand_107_out,
       nand_108_out, nand_109_out, nand_110_out, nand_111_out, nand_112_out, nand_113_out, nand_114_out,
       nand_115_out, nand_116_out, nand_117_out, nand_119_out, nand_120_out, nand_121_out, nand_122_out,
       nand_123_out, nand_124_out, nand_125_out, nand_126_out, nand_127_out, nand_128_out, nand_129_out,
       nand_130_out, nand_131_out, nand_132_out, nand_133_out, nand_135_out, nand_136_out, nand_137_out,
       nand_138_out, nand_139_out, nand_140_out, nand_141_out, nand_142_out, nand_143_out, nand_144_out,
       nand_145_out, nand_146_out, nand_147_out, nand_148_out, nand_149_out, nand_150_out, nand_151_out,
       nand_152_out, nand_153_out, nand_155_out, nand_156_out, nand_159_out, nand_160_out, nand_161_out,
       nand_165_out, nand_166_out, nand_167_out, nand_168_out;

  nand nand_1 (nand_1_out, read, read);
  nand nand_2 (nand_2_out, write, write);
  nand nand_3 (nand_3_out, isFound, isFound);
  nand nand_4 (nand_4_out, x1, x1);
  nand nand_5 (nand_5_out, read, read);
  nand nand_6 (nand_6_out, x1, x1);
  nand nand_7 (nand_7_out, write, write);
  nand nand_8 (nand_8_out, x2, x2);
  nand nand_9 (nand_9_out, x2, x2);
  nand nand_10 (nand_10_out, x0, x0);
  nand nand_11 (nand_11_out, read, read);
  nand nand_12 (nand_12_out, x2, x2);
  nand nand_13 (nand_13_out, x2, x2);
  nand nand_14 (nand_14_out, x2, x2);
  nand nand_15 (nand_15_out, x1, x1);
  nand nand_16 (nand_16_out, x2, x2);
  nand nand_17 (nand_17_out, x2, x2);
  nand nand_18 (nand_18_out, x2, x2);
  nand nand_19 (nand_19_out, nand_1_out, nand_2_out);
  nand nand_20 (nand_20_out, x1, nand_3_out);
  nand nand_21 (nand_21_out, nand_4_out, x0);
  nand nand_22 (nand_22_out, nand_5_out, write);
  nand nand_23 (nand_23_out, nand_6_out, x0);
  nand nand_24 (nand_24_out, read, nand_7_out);
  nand nand_25 (nand_25_out, nand_8_out, x1);
  nand nand_26 (nand_26_out, nand_9_out, x1);
  nand nand_27 (nand_27_out, x2, x1);
  nand nand_28 (nand_28_out, nand_10_out, nand_11_out);
  nand nand_29 (nand_29_out, nand_12_out, x1);
  nand nand_30 (nand_30_out, nand_13_out, x1);
  nand nand_31 (nand_31_out, nand_14_out, nand_15_out);
  nand nand_32 (nand_32_out, nand_16_out, x1);
  nand nand_33 (nand_33_out, x0, isFound);
  nand nand_34 (nand_34_out, nand_17_out, x1);
  nand nand_35 (nand_35_out, nand_18_out, x1);
  nand nand_36 (nand_36_out, x0, nand_19_out);
  nand nand_37 (nand_37_out, nand_20_out, nand_20_out);
  nand nand_38 (nand_38_out, isDirty, isDirty);
  nand nand_39 (nand_39_out, nand_21_out, nand_21_out);
  nand nand_40 (nand_40_out, nand_22_out, nand_22_out);
  nand nand_41 (nand_41_out, nand_23_out, nand_23_out);
  nand nand_42 (nand_42_out, nand_24_out, nand_24_out);
  nand nand_43 (nand_43_out, x2, x2);
  nand nand_44 (nand_44_out, x0, x0);
  nand nand_45 (nand_45_out, x2, x2);
  nand nand_46 (nand_46_out, nand_25_out, nand_25_out);
  nand nand_47 (nand_47_out, x1, x1);
  nand nand_48 (nand_48_out, x0, x0);
  nand nand_49 (nand_49_out, nand_26_out, nand_26_out);
  nand nand_50 (nand_50_out, isFound, isFound);
  nand nand_51 (nand_51_out, isDirty, isDirty);
  nand nand_52 (nand_52_out, x1, x1);
  nand nand_53 (nand_53_out, nand_27_out, nand_27_out);
  nand nand_54 (nand_54_out, nand_28_out, nand_28_out);
  nand nand_55 (nand_55_out, nand_29_out, nand_29_out);
  nand nand_56 (nand_56_out, isFound, isFound);
  nand nand_57 (nand_57_out, isDirty, isDirty);
  nand nand_58 (nand_58_out, x1, x1);
  nand nand_59 (nand_59_out, nand_30_out, nand_30_out);
  nand nand_60 (nand_60_out, isFound, isFound);
  nand nand_61 (nand_61_out, isDirty, isDirty);
  nand nand_62 (nand_62_out, x1, x1);
  nand nand_63 (nand_63_out, nand_31_out, nand_31_out);
  nand nand_64 (nand_64_out, x0, x0);
  nand nand_65 (nand_65_out, nand_32_out, nand_32_out);
  nand nand_66 (nand_66_out, nand_33_out, nand_33_out);
  nand nand_67 (nand_67_out, x1, x1);
  nand nand_68 (nand_68_out, nand_34_out, nand_34_out);
  nand nand_69 (nand_69_out, isFound, isFound);
  nand nand_70 (nand_70_out, isDirty, isDirty);
  nand nand_71 (nand_71_out, x1, x1);
  nand nand_72 (nand_72_out, nand_35_out, nand_35_out);
  nand nand_73 (nand_73_out, x0, x0);
  nand nand_74 (nand_74_out, nand_36_out, nand_36_out);
  nand nand_75 (nand_75_out, read, write);
  nand nand_76 (nand_76_out, nand_37_out, nand_38_out);
  nand nand_77 (nand_77_out, x2, x1);
  nand nand_78 (nand_78_out, nand_39_out, nand_40_out);
  nand nand_79 (nand_79_out, nand_41_out, nand_42_out);
  nand nand_80 (nand_80_out, nand_43_out, x1);
  nand nand_81 (nand_81_out, x1, nand_44_out);
  nand nand_82 (nand_82_out, nand_45_out, x1);
  nand nand_83 (nand_83_out, nand_46_out, x0);
  nand nand_84 (nand_84_out, x2, nand_47_out);
  nand nand_85 (nand_85_out, x2, nand_48_out);
  nand nand_86 (nand_86_out, nand_49_out, x0);
  nand nand_87 (nand_87_out, nand_50_out, nand_51_out);
  nand nand_88 (nand_88_out, x2, nand_52_out);
  nand nand_89 (nand_89_out, nand_53_out, nand_54_out);
  nand nand_90 (nand_90_out, nand_55_out, x0);
  nand nand_91 (nand_91_out, nand_56_out, nand_57_out);
  nand nand_92 (nand_92_out, x2, nand_58_out);
  nand nand_93 (nand_93_out, nand_59_out, x0);
  nand nand_94 (nand_94_out, nand_60_out, nand_61_out);
  nand nand_95 (nand_95_out, x2, nand_62_out);
  nand nand_96 (nand_96_out, nand_63_out, nand_64_out);
  nand nand_97 (nand_97_out, nand_65_out, nand_66_out);
  nand nand_98 (nand_98_out, x2, nand_67_out);
  nand nand_99 (nand_99_out, nand_68_out, x0);
  nand nand_100 (nand_100_out, nand_69_out, nand_70_out);
  nand nand_101 (nand_101_out, x2, nand_71_out);
  nand nand_102 (nand_102_out, nand_72_out, nand_73_out);
  nand nand_103 (nand_103_out, nand_74_out, nand_75_out);
  nand nand_104 (nand_104_out, nand_76_out, nand_77_out);
  nand nand_105 (nand_105_out, nand_78_out, nand_79_out);
  nand nand_106 (nand_106_out, nand_80_out, nand_80_out);
  nand nand_107 (nand_107_out, x0, x0);
  nand nand_108 (nand_108_out, nand_81_out, nand_81_out);
  nand nand_109 (nand_109_out, read, read);
  nand nand_110 (nand_110_out, nand_82_out, nand_82_out);
  nand nand_111 (nand_111_out, nand_83_out, nand_84_out);
  nand nand_112 (nand_112_out, nand_85_out, nand_85_out);
  nand nand_113 (nand_113_out, read, read);
  nand nand_114 (nand_114_out, nand_86_out, nand_86_out);
  nand nand_115 (nand_115_out, nand_87_out, nand_87_out);
  nand nand_116 (nand_116_out, nand_88_out, nand_88_out);
  nand nand_117 (nand_117_out, x0, x0);
  nand nand_118 (writeVal, nand_89_out, nand_89_out);
  nand nand_119 (nand_119_out, nand_90_out, nand_90_out);
  nand nand_120 (nand_120_out, nand_91_out, nand_91_out);
  nand nand_121 (nand_121_out, nand_92_out, nand_92_out);
  nand nand_122 (nand_122_out, x0, x0);
  nand nand_123 (nand_123_out, x0, x0);
  nand nand_124 (nand_124_out, nand_93_out, nand_93_out);
  nand nand_125 (nand_125_out, nand_94_out, nand_94_out);
  nand nand_126 (nand_126_out, nand_95_out, nand_95_out);
  nand nand_127 (nand_127_out, x0, x0);
  nand nand_128 (nand_128_out, nand_96_out, nand_97_out);
  nand nand_129 (nand_129_out, nand_98_out, nand_98_out);
  nand nand_130 (nand_130_out, nand_99_out, nand_99_out);
  nand nand_131 (nand_131_out, nand_100_out, nand_100_out);
  nand nand_132 (nand_132_out, nand_101_out, nand_101_out);
  nand nand_133 (nand_133_out, x0, x0);
  nand nand_134 (saveBlock, nand_102_out, nand_102_out);
  nand nand_135 (nand_135_out, nand_103_out, nand_103_out);
  nand nand_136 (nand_136_out, nand_104_out, nand_104_out);
  nand nand_137 (nand_137_out, nand_105_out, nand_105_out);
  nand nand_138 (nand_138_out, nand_106_out, nand_107_out);
  nand nand_139 (nand_139_out, nand_108_out, nand_109_out);
  nand nand_140 (nand_140_out, nand_110_out, isFound);
  nand nand_141 (nand_141_out, nand_111_out, nand_111_out);
  nand nand_142 (nand_142_out, nand_112_out, nand_113_out);
  nand nand_143 (nand_143_out, nand_114_out, nand_115_out);
  nand nand_144 (nand_144_out, nand_116_out, nand_117_out);
  nand nand_145 (nand_145_out, nand_119_out, nand_120_out);
  nand nand_146 (nand_146_out, nand_121_out, nand_122_out);
  nand nand_147 (nand_147_out, x2, nand_123_out);
  nand nand_148 (nand_148_out, nand_124_out, nand_125_out);
  nand nand_149 (nand_149_out, nand_126_out, nand_127_out);
  nand nand_150 (nand_150_out, nand_128_out, nand_128_out);
  nand nand_151 (nand_151_out, nand_129_out, x0);
  nand nand_152 (nand_152_out, nand_130_out, nand_131_out);
  nand nand_153 (nand_153_out, nand_132_out, nand_133_out);
  nand nand_154 (y2, nand_135_out, nand_136_out);
  nand nand_155 (nand_155_out, nand_137_out, nand_138_out);
  nand nand_156 (nand_156_out, nand_139_out, nand_140_out);
  nand nand_157 (y0, nand_141_out, nand_142_out);
  nand nand_158 (writeTo, nand_143_out, nand_144_out);
  nand nand_159 (nand_159_out, nand_145_out, nand_146_out);
  nand nand_160 (nand_160_out, nand_147_out, nand_147_out);
  nand nand_161 (nand_161_out, read, read);
  nand nand_162 (validNew, nand_148_out, nand_149_out);
  nand nand_163 (ageNew, nand_150_out, nand_151_out);
  nand nand_164 (tagNew, nand_152_out, nand_153_out);
  nand nand_165 (nand_165_out, nand_155_out, nand_155_out);
  nand nand_166 (nand_166_out, nand_156_out, nand_156_out);
  nand nand_167 (nand_167_out, nand_159_out, nand_159_out);
  nand nand_168 (nand_168_out, nand_160_out, nand_161_out);
  nand nand_169 (y1, nand_165_out, nand_166_out);
  nand nand_170 (dirtyNew, nand_167_out, nand_168_out);
endmodule
