// Logisim project NIC.circ as structural Verilog: 9 circuits, main circuit NIC
module main (
  input  En_Noise
);

  wire CLK, keyboard_1_avail, multiplexer_1_out, nic_1_int, nic_1_tx, noisychannel_1_out,
       terminalcontroller_1_cs, terminalcontroller_1_kben, terminalcontroller_1_o,
       terminalcontroller_1_ttyen, terminalcontroller_1_w;
  wire [1:0] terminalcontroller_1_addr;
  wire [6:0] keyboard_1_data, terminalcontroller_1_ttydata;
  wire [7:0] nic_1_dataout, terminalcontroller_1_dataout, terminalcontroller_1_status;

  TTY tty_1 (.data(terminalcontroller_1_ttydata), .clk(CLK), .we(terminalcontroller_1_ttyen));  // open: clr
  Keyboard keyboard_1 (
    .clk(CLK), .re(terminalcontroller_1_kben), .avail(keyboard_1_avail), .data(keyboard_1_data));  // open: clr
  LED DR (.in(terminalcontroller_1_status[1]));
  LED TBNF (.in(terminalcontroller_1_status[2]));
  LED TXI (.in(terminalcontroller_1_status[3]));
  LED NF (.in(terminalcontroller_1_status[4]));
  LED OR (.in(terminalcontroller_1_status[5]));
  LED SDE (.in(terminalcontroller_1_status[6]));
  LED FE (.in(terminalcontroller_1_status[7]));
  Clock clock_1 (.out(CLK));
  TerminalController terminalcontroller_1 (
    .TTYEN(terminalcontroller_1_ttyen), .TTYDATA(terminalcontroller_1_ttydata),
    .STATUS(terminalcontroller_1_status), .KBEN(terminalcontroller_1_kben), .KBRDY(keyboard_1_avail),
    .KBDATA(keyboard_1_data), .CLK(CLK), .DIV(4'b0011), .INT(nic_1_int), .CS(terminalcontroller_1_cs),
    .O(terminalcontroller_1_o), .W(terminalcontroller_1_w), .ADDR(terminalcontroller_1_addr),
    .DATAOUT(terminalcontroller_1_dataout), .DATAIN(nic_1_dataout));
  NIC nic_1 (
    .INT(nic_1_int), .CS(terminalcontroller_1_cs), .O(terminalcontroller_1_o), .W(terminalcontroller_1_w),
    .ADDR(terminalcontroller_1_addr), .DATAIN(terminalcontroller_1_dataout), .DATAOUT(nic_1_dataout),
    .CLK(CLK), .TX(nic_1_tx), .RX(multiplexer_1_out));
  Shift_Register #(.length(32)) shift_register_1 (
    .in(nic_1_tx), .clk(CLK));  // open: shift, out, load, clr, d0, q0, d1, q1, d2, q2, d3, q3, d4, q4, d5, q5, d6, q6, d7, q7, d8, q8, d9, q9, d10, q10, d11, q11, d12, q12, d13, q13, d14, q14, d15, q15, d16, q16, d17, q17, d18, q18, d19, q19, d20, q20, d21, q21, d22, q22, d23, q23, d24, q24, d25, q25, d26, q26, d27, q27, d28, q28, d29, q29, d30, q30, d31, q31
  Shift_Register #(.length(32)) shift_register_2 (
    .in(multiplexer_1_out), .clk(CLK));  // open: shift, out, load, clr, d0, q0, d1, q1, d2, q2, d3, q3, d4, q4, d5, q5, d6, q6, d7, q7, d8, q8, d9, q9, d10, q10, d11, q11, d12, q12, d13, q13, d14, q14, d15, q15, d16, q16, d17, q17, d18, q18, d19, q19, d20, q20, d21, q21, d22, q22, d23, q23, d24, q24, d25, q25, d26, q26, d27, q27, d28, q28, d29, q29, d30, q30, d31, q31
  NoisyChannel noisychannel_1 (.In(nic_1_tx), .Rate(16'h800), .CLK(CLK), .Out(noisychannel_1_out));
  Multiplexer #(.enable("false")) multiplexer_1 (
    .in0(nic_1_tx), .in1(noisychannel_1_out), .out(multiplexer_1_out), .sel(En_Noise));

  // Notes on the sheet:
  //   Div
  //   Noise Rate
endmodule

module TerminalController (
  input  KBRDY,
  input  [6:0] KBDATA,
  input  INT,
  input  [7:0] DATAIN,
  input  CLK,
  input  [3:0] DIV,
  output KBEN,
  output CS,
  output O,
  output TTYEN,
  output W,
  output [6:0] TTYDATA,
  output [1:0] ADDR,
  output [7:0] STATUS,
  output [7:0] DATAOUT
);

  wire DOCHECKS, JMP, not_4_out, not_5_out, not_6_out, STATUSEN, TF, TTYDATAOUTSEL, TTYENP;
  wire [1:0] and_2_out, DATAOUTSEL;
  wire [7:0] DATABUSBYTE, INST, JUMPTARGET, multiplexer_1_out, multiplexer_3_out;
  wire [7:7] multiplexer_2_out;
  wire [23:11] rom_1_data;

  ROM #(.dataWidth(24)) rom_1 (
    .addr(INST),
    .data({rom_1_data[23:21], ADDR, KBEN, TTYENP, DATAOUTSEL, TTYDATAOUTSEL, rom_1_data[13:11], DOCHECKS, STATUSEN, JMP, DATABUSBYTE}),
    .sel(1'b1));
  not not_1 (W, rom_1_data[21]);
  not not_2 (O, rom_1_data[22]);
  not not_3 (CS, rom_1_data[23]);
  assign DATAOUT = not_4_out ? multiplexer_1_out : 8'bz;  // Controlled_Buffer controlled_buffer_1
  Multiplexer #(.select(2), .width(8), .enable("false")) multiplexer_1 (
    .in0({4'b0000, DIV}), .in1(DATABUSBYTE), .in2({1'b1, KBDATA}), .in3({8{1'b0}}), .out(multiplexer_1_out),
    .sel(DATAOUTSEL));
  not not_4 (not_4_out, W);
  Multiplexer #(.width(8), .enable("false")) multiplexer_2 (
    .in0(DATAIN), .in1(DATABUSBYTE), .out({multiplexer_2_out[7], TTYDATA}), .sel(TTYDATAOUTSEL));
  and and_1 (TTYEN, multiplexer_2_out[7], TTYENP);
  Counter counter_1 (.load(JMP), .D(JUMPTARGET), .count(not_5_out), .Q(INST), .clk(CLK));  // open: carry, clr
  not not_5 (not_5_out, JMP);
  Multiplexer #(.width(8), .enable("false")) multiplexer_3 (
    .in0(8'h20), .in1(8'h30), .out(multiplexer_3_out), .sel(TF));
  and and_2 (and_2_out[0], KBRDY, DOCHECKS);
  and and_3 (and_2_out[1], DOCHECKS, not_6_out);
  not not_6 (not_6_out, INT);
  Comparator #(.width(7), .mode("unsigned")) comparator_1 (.a(KBDATA), .b(7'b0001010), .eq(TF));  // open: gt, lt
  Register register_1 (.D(DATAIN), .en(STATUSEN), .Q(STATUS), .clk(CLK));  // open: clr
  Multiplexer #(.select(2), .width(8), .enable("false")) multiplexer_4 (
    .in0(DATABUSBYTE), .in1(multiplexer_3_out), .in2(8'h10), .in3(8'h10), .out(JUMPTARGET), .sel(and_2_out));

  // Other names for the same wires on the sheet: KBDATABUSBYTE[6:0] = KBDATA

  // Notes on the sheet:
  //   contents of rom_1 (hex, n*v repeats v):
  //   0 b80000 b80000 0 a88002 a88002 0 a08001 a08001 0 c00000 c00000 c00200 509 0 0 d00000 d00000 d20000
  //   109 12*0 b10000 b10000 b10000 40000 109 11*0 b10000 b10000 b10000 40000 a08003 a08003 109
endmodule

module NIC (
  input  CS,
  input  O,
  input  W,
  input  RX,
  input  [1:0] ADDR,
  input  [7:0] DATAIN,
  input  CLK,
  output INT,
  output TX,
  output [7:0] DATAOUT
);

  wire and_1_out, and_2_out, BRDHigh, nor_1_out, nor_2_out, nor_3_out, nor_4_out, or_1_out;
  wire [7:0] BRD_q, multiplexer_1_out;

  or or_1 (or_1_out, DATAIN[4], DATAIN[5], DATAIN[6], DATAIN[7]);
  and and_1 (and_1_out, DATAIN[0], nor_1_out);
  nor nor_1 (nor_1_out, DATAIN[1], DATAIN[2], DATAIN[3], DATAIN[4], DATAIN[5], DATAIN[6], DATAIN[7]);
  and and_2 (and_2_out, DATAIN[1], nor_2_out);
  nor nor_2 (nor_2_out, DATAIN[0], DATAIN[2], DATAIN[3], DATAIN[4], DATAIN[5], DATAIN[6], DATAIN[7]);
  Multiplexer #(.width(8), .enable("false")) multiplexer_1 (
    .in0(BRD_q), .in1(DATAIN), .out(multiplexer_1_out), .sel(nor_3_out));
  nor nor_3 (nor_3_out, or_1_out, and_1_out, and_2_out, nor_4_out);
  Register BRD (.D(multiplexer_1_out), .en(1'b1), .Q(BRD_q), .clk(CLK));  // open: clr
  nor nor_4 (nor_4_out, DATAIN[7], DATAIN[6], DATAIN[5], DATAIN[4], DATAIN[3], DATAIN[2], DATAIN[1], DATAIN[0]);
  BRDcounter brdcounter_1 (.BRD(BRD_q[3:0]), .CLK(CLK), .out_3(BRDHigh));

  // Notes on the sheet:
  //   nicdisable
endmodule

module NoisyChannel (
  input  [15:0] Rate,
  input  In,
  input  CLK,
  output Out
);

  wire Flip;
  wire [15:0] RNG;
  wire [31:0] adder_1_out, multiplier_1_out, SEED;

  xor xor_1 (Out, In, Flip);
  Multiplier #(.width(32)) multiplier_1 (.a(SEED), .b(32'h15a4e35), .out(multiplier_1_out));  // open: cin, cout
  Adder #(.width(32)) adder_1 (.a(multiplier_1_out), .b(32'h1), .out(adder_1_out));  // open: cin, cout
  Comparator #(.width(16), .mode("unsigned")) comparator_1 (.a(RNG), .b(Rate), .lt(Flip));  // open: gt, eq
  Register #(.width(32)) register_1 (.D(adder_1_out), .Q(SEED), .clk(CLK));  // open: en, clr
  assign RNG = SEED[15:0] ^ SEED[31:16];  // XOR_Gate xor_2, 16 bits wide
endmodule

module secded (
  input  [15:0] DataIn,
  output [21:0] Output
);

  xor odd_parity_1 (Output[1], DataIn[0], DataIn[1], DataIn[3], DataIn[4], DataIn[6], DataIn[8], DataIn[10], DataIn[11], DataIn[13], DataIn[15]);
  xor odd_parity_2 (Output[4], DataIn[1], DataIn[2], DataIn[3], DataIn[7], DataIn[8], DataIn[9], DataIn[10], DataIn[14], DataIn[15]);
  xor odd_parity_3 (Output[0], Output[1], Output[2], DataIn[0], Output[4], DataIn[1], DataIn[2], DataIn[3], Output[8], DataIn[4], DataIn[5], DataIn[6], DataIn[7], DataIn[8], DataIn[9], DataIn[10], Output[16], DataIn[11], DataIn[12], DataIn[13], DataIn[14], DataIn[15]);
  xor odd_parity_4 (Output[16], DataIn[11], DataIn[12], DataIn[13], DataIn[14], DataIn[15]);
  xor odd_parity_5 (Output[2], DataIn[0], DataIn[2], DataIn[3], DataIn[5], DataIn[6], DataIn[9], DataIn[10], DataIn[12], DataIn[13]);
  xor odd_parity_6 (Output[8], DataIn[4], DataIn[5], DataIn[6], DataIn[7], DataIn[8], DataIn[9], DataIn[10]);

  assign {Output[21:17], Output[15:9], Output[7:5], Output[3]} = DataIn;

  // Other names for the same wires on the sheet: P0 = Output[0]; P1 = Output[1]; P2 = Output[2]; Di1 = DataIn[0];
  //   P3 = Output[4]; Di2 = DataIn[1]; Di3 = DataIn[2]; Di4 = DataIn[3]; P4 = Output[8]; Di5 = DataIn[4];
  //   Di6 = DataIn[5]; Di7 = DataIn[6]; Di8 = DataIn[7]; Di9 = DataIn[8]; Di10 = DataIn[9]; Di11 = DataIn[10];
  //   P5 = Output[16]; Di12 = DataIn[11]; Di13 = DataIn[12]; Di14 = DataIn[13]; Di15 = DataIn[14]; Di16 = DataIn[15]
endmodule

module BRDcounter (
  input  CLK,
  input  [3:0] BRD,
  output out_3
);

  wire and_1_out, t_ff_1_q, t_ff_1_qn, t_ff_2_q, t_ff_2_qn, t_ff_3_q, t_ff_3_qn, t_ff_4_q, t_ff_4_qn,
       xnor_1_out, xnor_2_out, xnor_3_out, xnor_4_out;

  T_Flip_Flop t_ff_1 (.clk(CLK), .T(1'b1), .Q(t_ff_1_q), .Qn(t_ff_1_qn), .reset(and_1_out));  // open: preset, en
  xnor xnor_1 (xnor_1_out, BRD[0], t_ff_1_q);
  T_Flip_Flop t_ff_2 (.clk(t_ff_1_qn), .T(1'b1), .Q(t_ff_2_q), .Qn(t_ff_2_qn), .reset(and_1_out));  // open: preset, en
  xnor xnor_2 (xnor_2_out, BRD[1], t_ff_2_q);
  and and_1 (and_1_out, xnor_1_out, xnor_2_out, xnor_3_out, xnor_4_out);
  T_Flip_Flop t_ff_3 (.clk(t_ff_2_qn), .T(1'b1), .Q(t_ff_3_q), .Qn(t_ff_3_qn), .reset(and_1_out));  // open: preset, en
  xnor xnor_3 (xnor_3_out, BRD[2], t_ff_3_q);
  T_Flip_Flop t_ff_4 (.clk(t_ff_3_qn), .T(1'b1), .Q(t_ff_4_q), .Qn(t_ff_4_qn), .reset(and_1_out));  // open: preset, en
  xnor xnor_4 (xnor_4_out, BRD[3], t_ff_4_q);
  and and_2 (out_3, t_ff_1_qn, t_ff_2_qn, t_ff_3_qn, t_ff_4_qn);
endmodule

module FIFO (
  input  CLK,
  input  Serial_Input,
  input  Shift_In,
  input  Parallel_Loading,
  input  [4:0] Parallel_Count,
  input  Serial_Output,
  input  Shift_Out__Input,
  input  [4:0] Count,
  input  Parallel_Unload,
  input  [21:0] Parallel_Output,
  input  [21:0] Parallel_Input,
  output [4:0] Count_Output
);

  wire multiplexer_1_out, multiplexer_2_out, multiplexer_4_out, multiplexer_6_out, multiplexer_7_out,
       multiplexer_8_out, multiplexer_9_out, multiplexer_10_out, multiplexer_11_out, multiplexer_12_out,
       multiplexer_13_out, multiplexer_14_out, multiplexer_15_out, multiplexer_16_out, multiplexer_17_out,
       multiplexer_18_out, multiplexer_19_out, multiplexer_20_out, multiplexer_21_out, multiplexer_22_out,
       multiplexer_23_out, multiplexer_24_out, multiplexer_25_out, multiplexer_26_out, multiplexer_27_out,
       multiplexer_28_out, multiplexer_29_out, multiplexer_30_out, multiplexer_31_out, multiplexer_32_out,
       multiplexer_33_out, multiplexer_34_out, multiplexer_35_out, multiplexer_36_out, multiplexer_37_out,
       multiplexer_38_out, multiplexer_39_out, multiplexer_40_out, multiplexer_41_out, multiplexer_42_out,
       multiplexer_43_out, multiplexer_44_out, multiplexer_45_out, multiplexer_46_out;
  wire [4:0] adder_1_out, and_1_out, and_2_out, and_3_out, and_4_out, and_5_out, and_6_out, and_7_out,
       and_8_out, and_9_out, and_10_out, and_11_out, and_12_out, and_13_out, and_14_out, and_15_out,
       and_16_out, and_17_out, and_18_out, and_19_out, and_20_out, and_21_out, and_22_out, subtractor_1_out,
       undriven;

  Multiplexer #(.select(5)) multiplexer_1 (
    .in0(Parallel_Output[21]), .in31(Serial_Input), .out(multiplexer_1_out), .sel(and_1_out));  // open: in1, in2, in3, in4, in5, in6, in7, in8, in9, in10, in11, in12, in13, in14, in15, in16, in17, in18, in19, in20, in21, in22, in23, in24, in25, in26, in27, in28, in29, in30, en
  assign and_1_out = Count & {5{1'b0}};  // AND_Gate and_1, 5 bits wide
  Multiplexer #(.select(3)) multiplexer_2 (
    .in0(Parallel_Output[21]), .in1(Parallel_Input[21]), .in2(Parallel_Output[20]), .in3(Parallel_Input[21]),
    .in4(multiplexer_1_out), .in5(Parallel_Input[21]), .in7(Parallel_Input[21]), .out(multiplexer_2_out),
    .sel({Shift_In, Shift_Out__Input, Parallel_Loading}));  // open: in6, en
  D_Flip_Flop d_ff_1 (.clk(CLK), .D(multiplexer_2_out), .Q(Parallel_Output[21]));  // open: Qn, preset, en, reset
  Multiplexer multiplexer_3 (.in1(Parallel_Output[21]), .out(Serial_Output), .sel(Shift_Out__Input));  // open: in0, en
  Subtractor #(.width(5)) subtractor_1 (.a(Count_Output), .b(5'b00001), .out(subtractor_1_out));  // open: bin, bout
  Multiplexer #(.select(5)) multiplexer_4 (
    .in0(Parallel_Output[20]), .in31(Serial_Input), .out(multiplexer_4_out), .sel(and_2_out));  // open: in1, in2, in3, in4, in5, in6, in7, in8, in9, in10, in11, in12, in13, in14, in15, in16, in17, in18, in19, in20, in21, in22, in23, in24, in25, in26, in27, in28, in29, in30, en
  Adder #(.width(5)) adder_1 (.a(Count_Output), .b(5'b00001), .out(adder_1_out));  // open: cin, cout
  assign and_2_out = Count & 5'b00001;  // AND_Gate and_2, 5 bits wide
  Multiplexer #(.select(4), .width(5)) multiplexer_5 (
    .in1({5{1'b0}}), .in2(subtractor_1_out), .in4(adder_1_out), .in8(Parallel_Count), .in10(undriven),
    .in11(undriven), .out(Count_Output), .sel({Parallel_Loading, Shift_In, Shift_Out__Input, Parallel_Unload}));  // open: in0, in3, in5, in6, in7, in9, in12, in13, in14, in15, en
  Multiplexer #(.select(3)) multiplexer_6 (
    .in0(Parallel_Output[20]), .in1(Parallel_Input[20]), .in2(Parallel_Output[19]), .in3(Parallel_Input[20]),
    .in4(multiplexer_4_out), .in5(Parallel_Input[20]), .in7(Parallel_Input[20]), .out(multiplexer_6_out),
    .sel({Shift_In, Shift_Out__Input, Parallel_Loading}));  // open: in6, en
  D_Flip_Flop d_ff_2 (.clk(CLK), .D(multiplexer_6_out), .Q(Parallel_Output[20]));  // open: Qn, preset, en, reset
  Multiplexer #(.select(5)) multiplexer_7 (
    .in0(Parallel_Output[19]), .in31(Serial_Input), .out(multiplexer_7_out), .sel(and_3_out));  // open: in1, in2, in3, in4, in5, in6, in7, in8, in9, in10, in11, in12, in13, in14, in15, in16, in17, in18, in19, in20, in21, in22, in23, in24, in25, in26, in27, in28, in29, in30, en
  assign and_3_out = Count & 5'b00010;  // AND_Gate and_3, 5 bits wide
  Multiplexer #(.select(3)) multiplexer_8 (
    .in0(Parallel_Output[19]), .in1(Parallel_Input[19]), .in2(Parallel_Output[18]), .in3(Parallel_Input[19]),
    .in4(multiplexer_7_out), .in5(Parallel_Input[19]), .in7(Parallel_Input[19]), .out(multiplexer_8_out),
    .sel({Shift_In, Shift_Out__Input, Parallel_Loading}));  // open: in6, en
  D_Flip_Flop d_ff_3 (.clk(CLK), .D(multiplexer_8_out), .Q(Parallel_Output[19]));  // open: Qn, preset, en, reset
  Multiplexer #(.select(5)) multiplexer_9 (
    .in0(Parallel_Output[18]), .in31(Serial_Input), .out(multiplexer_9_out), .sel(and_4_out));  // open: in1, in2, in3, in4, in5, in6, in7, in8, in9, in10, in11, in12, in13, in14, in15, in16, in17, in18, in19, in20, in21, in22, in23, in24, in25, in26, in27, in28, in29, in30, en
  assign and_4_out = Count & 5'b00011;  // AND_Gate and_4, 5 bits wide
  Multiplexer #(.select(3)) multiplexer_10 (
    .in0(Parallel_Output[18]), .in1(Parallel_Input[18]), .in2(Parallel_Output[17]), .in3(Parallel_Input[18]),
    .in4(multiplexer_9_out), .in5(Parallel_Input[18]), .in7(Parallel_Input[18]), .out(multiplexer_10_out),
    .sel({Shift_In, Shift_Out__Input, Parallel_Loading}));  // open: in6, en
  D_Flip_Flop d_ff_4 (.clk(CLK), .D(multiplexer_10_out), .Q(Parallel_Output[18]));  // open: Qn, preset, en, reset
  Multiplexer #(.select(5)) multiplexer_11 (
    .in0(Parallel_Output[17]), .in31(Serial_Input), .out(multiplexer_11_out), .sel(and_5_out));  // open: in1, in2, in3, in4, in5, in6, in7, in8, in9, in10, in11, in12, in13, in14, in15, in16, in17, in18, in19, in20, in21, in22, in23, in24, in25, in26, in27, in28, in29, in30, en
  assign and_5_out = Count & 5'b00100;  // AND_Gate and_5, 5 bits wide
  Multiplexer #(.select(3)) multiplexer_12 (
    .in0(Parallel_Output[17]), .in1(Parallel_Input[17]), .in2(Parallel_Output[16]), .in3(Parallel_Input[17]),
    .in4(multiplexer_11_out), .in5(Parallel_Input[17]), .in7(Parallel_Input[17]), .out(multiplexer_12_out),
    .sel({Shift_In, Shift_Out__Input, Parallel_Loading}));  // open: in6, en
  D_Flip_Flop d_ff_5 (.clk(CLK), .D(multiplexer_12_out), .Q(Parallel_Output[17]));  // open: Qn, preset, en, reset
  Multiplexer #(.select(5)) multiplexer_13 (
    .in0(Parallel_Output[16]), .in31(Serial_Input), .out(multiplexer_13_out), .sel(and_6_out));  // open: in1, in2, in3, in4, in5, in6, in7, in8, in9, in10, in11, in12, in13, in14, in15, in16, in17, in18, in19, in20, in21, in22, in23, in24, in25, in26, in27, in28, in29, in30, en
  assign and_6_out = Count & 5'b00101;  // AND_Gate and_6, 5 bits wide
  Multiplexer #(.select(3)) multiplexer_14 (
    .in0(Parallel_Output[16]), .in1(Parallel_Input[16]), .in2(Parallel_Output[15]), .in3(Parallel_Input[16]),
    .in4(multiplexer_13_out), .in5(Parallel_Input[16]), .in7(Parallel_Input[16]), .out(multiplexer_14_out),
    .sel({Shift_In, Shift_Out__Input, Parallel_Loading}));  // open: in6, en
  D_Flip_Flop d_ff_6 (.clk(CLK), .D(multiplexer_14_out), .Q(Parallel_Output[16]));  // open: Qn, preset, en, reset
  Multiplexer #(.select(5)) multiplexer_15 (
    .in0(Parallel_Output[15]), .in31(Serial_Input), .out(multiplexer_15_out), .sel(and_7_out));  // open: in1, in2, in3, in4, in5, in6, in7, in8, in9, in10, in11, in12, in13, in14, in15, in16, in17, in18, in19, in20, in21, in22, in23, in24, in25, in26, in27, in28, in29, in30, en
  assign and_7_out = Count & 5'b00110;  // AND_Gate and_7, 5 bits wide
  Multiplexer #(.select(3)) multiplexer_16 (
    .in0(Parallel_Output[15]), .in1(Parallel_Input[15]), .in2(Parallel_Output[14]), .in3(Parallel_Input[15]),
    .in4(multiplexer_15_out), .in5(Parallel_Input[15]), .in7(Parallel_Input[15]), .out(multiplexer_16_out),
    .sel({Shift_In, Shift_Out__Input, Parallel_Loading}));  // open: in6, en
  D_Flip_Flop d_ff_7 (.clk(CLK), .D(multiplexer_16_out), .Q(Parallel_Output[15]));  // open: Qn, preset, en, reset
  Multiplexer #(.select(5)) multiplexer_17 (
    .in0(Parallel_Output[14]), .in31(Serial_Input), .out(multiplexer_17_out), .sel(and_8_out));  // open: in1, in2, in3, in4, in5, in6, in7, in8, in9, in10, in11, in12, in13, in14, in15, in16, in17, in18, in19, in20, in21, in22, in23, in24, in25, in26, in27, in28, in29, in30, en
  assign and_8_out = Count & 5'b00111;  // AND_Gate and_8, 5 bits wide
  Multiplexer #(.select(3)) multiplexer_18 (
    .in0(Parallel_Output[14]), .in1(Parallel_Input[14]), .in2(Parallel_Output[13]), .in3(Parallel_Input[14]),
    .in4(multiplexer_17_out), .in5(Parallel_Input[14]), .in7(Parallel_Input[14]), .out(multiplexer_18_out),
    .sel({Shift_In, Shift_Out__Input, Parallel_Loading}));  // open: in6, en
  D_Flip_Flop d_ff_8 (.clk(CLK), .D(multiplexer_18_out), .Q(Parallel_Output[14]));  // open: Qn, preset, en, reset
  Multiplexer #(.select(5)) multiplexer_19 (
    .in0(Parallel_Output[13]), .in31(Serial_Input), .out(multiplexer_19_out), .sel(and_9_out));  // open: in1, in2, in3, in4, in5, in6, in7, in8, in9, in10, in11, in12, in13, in14, in15, in16, in17, in18, in19, in20, in21, in22, in23, in24, in25, in26, in27, in28, in29, in30, en
  assign and_9_out = Count & 5'b01000;  // AND_Gate and_9, 5 bits wide
  Multiplexer #(.select(3)) multiplexer_20 (
    .in0(Parallel_Output[13]), .in1(Parallel_Input[13]), .in2(Parallel_Output[12]), .in3(Parallel_Input[13]),
    .in4(multiplexer_19_out), .in5(Parallel_Input[13]), .in7(Parallel_Input[13]), .out(multiplexer_20_out),
    .sel({Shift_In, Shift_Out__Input, Parallel_Loading}));  // open: in6, en
  D_Flip_Flop d_ff_9 (.clk(CLK), .D(multiplexer_20_out), .Q(Parallel_Output[13]));  // open: Qn, preset, en, reset
  Multiplexer #(.select(5)) multiplexer_21 (
    .in0(Parallel_Output[12]), .in31(Serial_Input), .out(multiplexer_21_out), .sel(and_10_out));  // open: in1, in2, in3, in4, in5, in6, in7, in8, in9, in10, in11, in12, in13, in14, in15, in16, in17, in18, in19, in20, in21, in22, in23, in24, in25, in26, in27, in28, in29, in30, en
  assign and_10_out = Count & 5'b01001;  // AND_Gate and_10, 5 bits wide
  Multiplexer #(.select(3)) multiplexer_22 (
    .in0(Parallel_Output[12]), .in1(Parallel_Input[12]), .in2(Parallel_Output[11]), .in3(Parallel_Input[12]),
    .in4(multiplexer_21_out), .in5(Parallel_Input[12]), .in7(Parallel_Input[12]), .out(multiplexer_22_out),
    .sel({Shift_In, Shift_Out__Input, Parallel_Loading}));  // open: in6, en
  D_Flip_Flop d_ff_10 (.clk(CLK), .D(multiplexer_22_out), .Q(Parallel_Output[12]));  // open: Qn, preset, en, reset
  Multiplexer #(.select(5)) multiplexer_23 (
    .in0(Parallel_Output[11]), .in31(Serial_Input), .out(multiplexer_23_out), .sel(and_11_out));  // open: in1, in2, in3, in4, in5, in6, in7, in8, in9, in10, in11, in12, in13, in14, in15, in16, in17, in18, in19, in20, in21, in22, in23, in24, in25, in26, in27, in28, in29, in30, en
  assign and_11_out = Count & 5'b01010;  // AND_Gate and_11, 5 bits wide
  Multiplexer #(.select(3)) multiplexer_24 (
    .in0(Parallel_Output[11]), .in1(Parallel_Input[11]), .in2(Parallel_Output[10]), .in3(Parallel_Input[11]),
    .in4(multiplexer_23_out), .in5(Parallel_Input[11]), .in7(Parallel_Input[11]), .out(multiplexer_24_out),
    .sel({Shift_In, Shift_Out__Input, Parallel_Loading}));  // open: in6, en
  D_Flip_Flop d_ff_11 (.clk(CLK), .D(multiplexer_24_out), .Q(Parallel_Output[11]));  // open: Qn, preset, en, reset
  Multiplexer #(.select(5)) multiplexer_25 (
    .in0(Parallel_Output[10]), .in31(Serial_Input), .out(multiplexer_25_out), .sel(and_12_out));  // open: in1, in2, in3, in4, in5, in6, in7, in8, in9, in10, in11, in12, in13, in14, in15, in16, in17, in18, in19, in20, in21, in22, in23, in24, in25, in26, in27, in28, in29, in30, en
  assign and_12_out = Count & 5'b01011;  // AND_Gate and_12, 5 bits wide
  Multiplexer #(.select(3)) multiplexer_26 (
    .in0(Parallel_Output[10]), .in1(Parallel_Input[10]), .in2(Parallel_Output[9]), .in3(Parallel_Input[10]),
    .in4(multiplexer_25_out), .in5(Parallel_Input[10]), .in7(Parallel_Input[10]), .out(multiplexer_26_out),
    .sel({Shift_In, Shift_Out__Input, Parallel_Loading}));  // open: in6, en
  D_Flip_Flop d_ff_12 (.clk(CLK), .D(multiplexer_26_out), .Q(Parallel_Output[10]));  // open: Qn, preset, en, reset
  Multiplexer #(.select(5)) multiplexer_27 (
    .in0(Parallel_Output[9]), .in31(Serial_Input), .out(multiplexer_27_out), .sel(and_13_out));  // open: in1, in2, in3, in4, in5, in6, in7, in8, in9, in10, in11, in12, in13, in14, in15, in16, in17, in18, in19, in20, in21, in22, in23, in24, in25, in26, in27, in28, in29, in30, en
  assign and_13_out = Count & 5'b01100;  // AND_Gate and_13, 5 bits wide
  Multiplexer #(.select(3)) multiplexer_28 (
    .in0(Parallel_Output[9]), .in1(Parallel_Input[9]), .in2(Parallel_Output[8]), .in3(Parallel_Input[9]),
    .in4(multiplexer_27_out), .in5(Parallel_Input[9]), .in7(Parallel_Input[9]), .out(multiplexer_28_out),
    .sel({Shift_In, Shift_Out__Input, Parallel_Loading}));  // open: in6, en
  D_Flip_Flop d_ff_13 (.clk(CLK), .D(multiplexer_28_out), .Q(Parallel_Output[9]));  // open: Qn, preset, en, reset
  Multiplexer #(.select(5)) multiplexer_29 (
    .in0(Parallel_Output[8]), .in31(Serial_Input), .out(multiplexer_29_out), .sel(and_14_out));  // open: in1, in2, in3, in4, in5, in6, in7, in8, in9, in10, in11, in12, in13, in14, in15, in16, in17, in18, in19, in20, in21, in22, in23, in24, in25, in26, in27, in28, in29, in30, en
  assign and_14_out = Count & 5'b01101;  // AND_Gate and_14, 5 bits wide
  Multiplexer #(.select(3)) multiplexer_30 (
    .in0(Parallel_Output[8]), .in1(Parallel_Input[8]), .in2(Parallel_Output[7]), .in3(Parallel_Input[8]),
    .in4(multiplexer_29_out), .in5(Parallel_Input[8]), .in7(Parallel_Input[8]), .out(multiplexer_30_out),
    .sel({Shift_In, Shift_Out__Input, Parallel_Loading}));  // open: in6, en
  D_Flip_Flop d_ff_14 (.clk(CLK), .D(multiplexer_30_out), .Q(Parallel_Output[8]));  // open: Qn, preset, en, reset
  Multiplexer #(.select(5)) multiplexer_31 (
    .in0(Parallel_Output[7]), .in31(Serial_Input), .out(multiplexer_31_out), .sel(and_15_out));  // open: in1, in2, in3, in4, in5, in6, in7, in8, in9, in10, in11, in12, in13, in14, in15, in16, in17, in18, in19, in20, in21, in22, in23, in24, in25, in26, in27, in28, in29, in30, en
  assign and_15_out = Count & 5'b01110;  // AND_Gate and_15, 5 bits wide
  Multiplexer #(.select(3)) multiplexer_32 (
    .in0(Parallel_Output[7]), .in1(Parallel_Input[7]), .in2(Parallel_Output[6]), .in3(Parallel_Input[7]),
    .in4(multiplexer_31_out), .in5(Parallel_Input[7]), .in7(Parallel_Input[7]), .out(multiplexer_32_out),
    .sel({Shift_In, Shift_Out__Input, Parallel_Loading}));  // open: in6, en
  D_Flip_Flop d_ff_15 (.clk(CLK), .D(multiplexer_32_out), .Q(Parallel_Output[7]));  // open: Qn, preset, en, reset
  Multiplexer #(.select(5)) multiplexer_33 (
    .in0(Parallel_Output[6]), .in31(Serial_Input), .out(multiplexer_33_out), .sel(and_16_out));  // open: in1, in2, in3, in4, in5, in6, in7, in8, in9, in10, in11, in12, in13, in14, in15, in16, in17, in18, in19, in20, in21, in22, in23, in24, in25, in26, in27, in28, in29, in30, en
  assign and_16_out = Count & 5'b01111;  // AND_Gate and_16, 5 bits wide
  Multiplexer #(.select(3)) multiplexer_34 (
    .in0(Parallel_Output[6]), .in1(Parallel_Input[6]), .in2(Parallel_Output[5]), .in3(Parallel_Input[6]),
    .in4(multiplexer_33_out), .in5(Parallel_Input[6]), .in7(Parallel_Input[6]), .out(multiplexer_34_out),
    .sel({Shift_In, Shift_Out__Input, Parallel_Loading}));  // open: in6, en
  D_Flip_Flop d_ff_16 (.clk(CLK), .D(multiplexer_34_out), .Q(Parallel_Output[6]));  // open: Qn, preset, en, reset
  Multiplexer #(.select(5)) multiplexer_35 (
    .in0(Parallel_Output[5]), .in31(Serial_Input), .out(multiplexer_35_out), .sel(and_17_out));  // open: in1, in2, in3, in4, in5, in6, in7, in8, in9, in10, in11, in12, in13, in14, in15, in16, in17, in18, in19, in20, in21, in22, in23, in24, in25, in26, in27, in28, in29, in30, en
  assign and_17_out = Count & 5'b10000;  // AND_Gate and_17, 5 bits wide
  Multiplexer #(.select(3)) multiplexer_36 (
    .in0(Parallel_Output[5]), .in1(Parallel_Input[5]), .in2(Parallel_Output[4]), .in3(Parallel_Input[5]),
    .in4(multiplexer_35_out), .in5(Parallel_Input[5]), .in7(Parallel_Input[5]), .out(multiplexer_36_out),
    .sel({Shift_In, Shift_Out__Input, Parallel_Loading}));  // open: in6, en
  D_Flip_Flop d_ff_17 (.clk(CLK), .D(multiplexer_36_out), .Q(Parallel_Output[5]));  // open: Qn, preset, en, reset
  Multiplexer #(.select(5)) multiplexer_37 (
    .in0(Parallel_Output[4]), .in31(Serial_Input), .out(multiplexer_37_out), .sel(and_18_out));  // open: in1, in2, in3, in4, in5, in6, in7, in8, in9, in10, in11, in12, in13, in14, in15, in16, in17, in18, in19, in20, in21, in22, in23, in24, in25, in26, in27, in28, in29, in30, en
  assign and_18_out = Count & 5'b10001;  // AND_Gate and_18, 5 bits wide
  Multiplexer #(.select(3)) multiplexer_38 (
    .in0(Parallel_Output[4]), .in1(Parallel_Input[4]), .in2(Parallel_Output[3]), .in3(Parallel_Input[4]),
    .in4(multiplexer_37_out), .in5(Parallel_Input[4]), .in7(Parallel_Input[4]), .out(multiplexer_38_out),
    .sel({Shift_In, Shift_Out__Input, Parallel_Loading}));  // open: in6, en
  D_Flip_Flop d_ff_18 (.clk(CLK), .D(multiplexer_38_out), .Q(Parallel_Output[4]));  // open: Qn, preset, en, reset
  Multiplexer #(.select(5)) multiplexer_39 (
    .in0(Parallel_Output[3]), .in31(Serial_Input), .out(multiplexer_39_out), .sel(and_19_out));  // open: in1, in2, in3, in4, in5, in6, in7, in8, in9, in10, in11, in12, in13, in14, in15, in16, in17, in18, in19, in20, in21, in22, in23, in24, in25, in26, in27, in28, in29, in30, en
  assign and_19_out = Count & 5'b10010;  // AND_Gate and_19, 5 bits wide
  Multiplexer #(.select(3)) multiplexer_40 (
    .in0(Parallel_Output[3]), .in1(Parallel_Input[3]), .in2(Parallel_Output[2]), .in3(Parallel_Input[3]),
    .in4(multiplexer_39_out), .in5(Parallel_Input[3]), .in7(Parallel_Input[3]), .out(multiplexer_40_out),
    .sel({Shift_In, Shift_Out__Input, Parallel_Loading}));  // open: in6, en
  D_Flip_Flop d_ff_19 (.clk(CLK), .D(multiplexer_40_out), .Q(Parallel_Output[3]));  // open: Qn, preset, en, reset
  Multiplexer #(.select(5)) multiplexer_41 (
    .in0(Parallel_Output[2]), .in31(Serial_Input), .out(multiplexer_41_out), .sel(and_20_out));  // open: in1, in2, in3, in4, in5, in6, in7, in8, in9, in10, in11, in12, in13, in14, in15, in16, in17, in18, in19, in20, in21, in22, in23, in24, in25, in26, in27, in28, in29, in30, en
  assign and_20_out = Count & 5'b10011;  // AND_Gate and_20, 5 bits wide
  Multiplexer #(.select(3)) multiplexer_42 (
    .in0(Parallel_Output[2]), .in1(Parallel_Input[2]), .in2(Parallel_Output[1]), .in3(Parallel_Input[2]),
    .in4(multiplexer_41_out), .in5(Parallel_Input[2]), .in7(Parallel_Input[2]), .out(multiplexer_42_out),
    .sel({Shift_In, Shift_Out__Input, Parallel_Loading}));  // open: in6, en
  D_Flip_Flop d_ff_20 (.clk(CLK), .D(multiplexer_42_out), .Q(Parallel_Output[2]));  // open: Qn, preset, en, reset
  Multiplexer #(.select(5)) multiplexer_43 (
    .in0(Parallel_Output[1]), .in31(Serial_Input), .out(multiplexer_43_out), .sel(and_21_out));  // open: in1, in2, in3, in4, in5, in6, in7, in8, in9, in10, in11, in12, in13, in14, in15, in16, in17, in18, in19, in20, in21, in22, in23, in24, in25, in26, in27, in28, in29, in30, en
  assign and_21_out = Count & 5'b10100;  // AND_Gate and_21, 5 bits wide
  Multiplexer #(.select(3)) multiplexer_44 (
    .in0(Parallel_Output[1]), .in1(Parallel_Input[1]), .in2(Parallel_Output[0]), .in3(Parallel_Input[1]),
    .in4(multiplexer_43_out), .in5(Parallel_Input[1]), .in7(Parallel_Input[1]), .out(multiplexer_44_out),
    .sel({Shift_In, Shift_Out__Input, Parallel_Loading}));  // open: in6, en
  D_Flip_Flop d_ff_21 (.clk(CLK), .D(multiplexer_44_out), .Q(Parallel_Output[1]));  // open: Qn, preset, en, reset
  Multiplexer #(.select(5)) multiplexer_45 (
    .in0(Parallel_Output[0]), .in31(Serial_Input), .out(multiplexer_45_out), .sel(and_22_out));  // open: in1, in2, in3, in4, in5, in6, in7, in8, in9, in10, in11, in12, in13, in14, in15, in16, in17, in18, in19, in20, in21, in22, in23, in24, in25, in26, in27, in28, in29, in30, en
  assign and_22_out = Count & 5'b10101;  // AND_Gate and_22, 5 bits wide
  Multiplexer #(.select(3)) multiplexer_46 (
    .in0(Parallel_Output[0]), .in1(Parallel_Input[0]), .in3(Parallel_Input[0]), .in4(multiplexer_45_out),
    .in5(Parallel_Input[0]), .in7(Parallel_Input[0]), .out(multiplexer_46_out),
    .sel({Shift_In, Shift_Out__Input, Parallel_Loading}));  // open: in2, in6, en
  D_Flip_Flop d_ff_22 (.clk(CLK), .D(multiplexer_46_out), .Q(Parallel_Output[0]));  // open: Qn, preset, en, reset

  // Other names for the same wires on the sheet: PU = Parallel_Unload; PL = Parallel_Loading; SHO = Shift_Out__Input;
  //   SHI = Shift_In; PC[4:0] = Parallel_Count; PI[21:0] = Parallel_Input; PI22 = Parallel_Input[0];
  //   PI21 = Parallel_Input[1]; PI20 = Parallel_Input[2]; PI19 = Parallel_Input[3]; PI18 = Parallel_Input[4];
  //   PI17 = Parallel_Input[5]; PI16 = Parallel_Input[6]; PI15 = Parallel_Input[7]; PI14 = Parallel_Input[8];
  //   PI13 = Parallel_Input[9]; PI12 = Parallel_Input[10]; PI11 = Parallel_Input[11]; PI10 = Parallel_Input[12];
  //   PI9 = Parallel_Input[13]; PI8 = Parallel_Input[14]; PI7 = Parallel_Input[15]; PI6 = Parallel_Input[16];
  //   PI5 = Parallel_Input[17]; PI4 = Parallel_Input[18]; PI3 = Parallel_Input[19]; PI2 = Parallel_Input[20];
  //   PI1 = Parallel_Input[21]; D22 = Parallel_Output[0]; PO[21:0] = Parallel_Output; PO22 = Parallel_Output[0];
  //   D21 = Parallel_Output[1]; PO21 = Parallel_Output[1]; D20 = Parallel_Output[2]; PO20 = Parallel_Output[2];
  //   D19 = Parallel_Output[3]; PO19 = Parallel_Output[3]; D18 = Parallel_Output[4]; PO18 = Parallel_Output[4];
  //   D17 = Parallel_Output[5]; PO17 = Parallel_Output[5]; D16 = Parallel_Output[6]; PO16 = Parallel_Output[6];
  //   D15 = Parallel_Output[7]; PO15 = Parallel_Output[7]; D14 = Parallel_Output[8]; PO14 = Parallel_Output[8];
  //   D13 = Parallel_Output[9]; PO13 = Parallel_Output[9]; D12 = Parallel_Output[10]; PO12 = Parallel_Output[10];
  //   D11 = Parallel_Output[11]; PO11 = Parallel_Output[11]; D10 = Parallel_Output[12]; PO10 = Parallel_Output[12];
  //   D9 = Parallel_Output[13]; PO9 = Parallel_Output[13]; D8 = Parallel_Output[14]; PO8 = Parallel_Output[14];
  //   D7 = Parallel_Output[15]; PO7 = Parallel_Output[15]; D6 = Parallel_Output[16]; PO6 = Parallel_Output[16];
  //   D5 = Parallel_Output[17]; PO5 = Parallel_Output[17]; D4 = Parallel_Output[18]; PO4 = Parallel_Output[18];
  //   D3 = Parallel_Output[19]; PO3 = Parallel_Output[19]; D2 = Parallel_Output[20]; PO2 = Parallel_Output[20];
  //   D1 = Parallel_Output[21]; PO1 = Parallel_Output[21]; SI = Serial_Input; SO = Serial_Output

  // Notes on the sheet:
  //   Can both be 1, parallel takes precedence 
  //   Push?
  //   Enable
  //   Enable
  //   How many bits we are about to parallel load
  //   Enable? Pop?
  //   Set Count to 0
  //   Take all bits and unload simultaneously
endmodule

module FIFO2 (
  input  CLK,
  input  Serial_Input,
  input  Shift_In,
  input  Parallel_Loading,
  input  [4:0] Parallel_Count,
  input  Serial_Output,
  input  Shift_Out__Input,
  input  [4:0] Count,
  input  Parallel_Unload,
  input  [21:0] Parallel_Output,
  input  [21:0] Parallel_Input,
  output [4:0] Count_Output
);

  wire multiplexer_1_out, multiplexer_2_out, multiplexer_4_out, multiplexer_6_out, multiplexer_7_out,
       multiplexer_8_out, multiplexer_9_out, multiplexer_10_out, multiplexer_11_out, multiplexer_12_out,
       multiplexer_13_out, multiplexer_14_out, multiplexer_15_out, multiplexer_16_out, multiplexer_17_out,
       multiplexer_18_out, multiplexer_19_out, multiplexer_20_out, multiplexer_21_out, multiplexer_22_out,
       multiplexer_23_out, multiplexer_24_out, multiplexer_25_out, multiplexer_26_out, multiplexer_27_out,
       multiplexer_28_out, multiplexer_29_out, multiplexer_30_out, multiplexer_31_out, multiplexer_32_out,
       multiplexer_33_out, multiplexer_34_out, multiplexer_35_out, multiplexer_36_out, multiplexer_37_out,
       multiplexer_38_out, multiplexer_39_out, multiplexer_40_out, multiplexer_41_out, multiplexer_42_out,
       multiplexer_43_out, multiplexer_44_out, multiplexer_45_out, multiplexer_46_out;
  wire [4:0] adder_1_out, and_1_out, and_2_out, and_3_out, and_4_out, and_5_out, and_6_out, and_7_out,
       and_8_out, and_9_out, and_10_out, and_11_out, and_12_out, and_13_out, and_14_out, and_15_out,
       and_16_out, and_17_out, and_18_out, and_19_out, and_20_out, and_21_out, and_22_out, subtractor_1_out,
       undriven;

  Multiplexer #(.select(5)) multiplexer_1 (
    .in0(Parallel_Output[21]), .in31(Serial_Input), .out(multiplexer_1_out), .sel(and_1_out));  // open: in1, in2, in3, in4, in5, in6, in7, in8, in9, in10, in11, in12, in13, in14, in15, in16, in17, in18, in19, in20, in21, in22, in23, in24, in25, in26, in27, in28, in29, in30, en
  assign and_1_out = Count & {5{1'b0}};  // AND_Gate and_1, 5 bits wide
  Multiplexer #(.select(3)) multiplexer_2 (
    .in0(Parallel_Output[21]), .in1(Parallel_Input[21]), .in2(Parallel_Output[20]), .in3(Parallel_Input[21]),
    .in4(multiplexer_1_out), .in5(Parallel_Input[21]), .in7(Parallel_Input[21]), .out(multiplexer_2_out),
    .sel({Shift_In, Shift_Out__Input, Parallel_Loading}));  // open: in6, en
  D_Flip_Flop d_ff_1 (.clk(CLK), .D(multiplexer_2_out), .Q(Parallel_Output[21]));  // open: Qn, preset, en, reset
  Multiplexer multiplexer_3 (.in1(Parallel_Output[21]), .out(Serial_Output), .sel(Shift_Out__Input));  // open: in0, en
  Subtractor #(.width(5)) subtractor_1 (.a(Count_Output), .b(5'b00001), .out(subtractor_1_out));  // open: bin, bout
  Multiplexer #(.select(5)) multiplexer_4 (
    .in0(Parallel_Output[20]), .in31(Serial_Input), .out(multiplexer_4_out), .sel(and_2_out));  // open: in1, in2, in3, in4, in5, in6, in7, in8, in9, in10, in11, in12, in13, in14, in15, in16, in17, in18, in19, in20, in21, in22, in23, in24, in25, in26, in27, in28, in29, in30, en
  Adder #(.width(5)) adder_1 (.a(Count_Output), .b(5'b00001), .out(adder_1_out));  // open: cin, cout
  assign and_2_out = Count & 5'b00001;  // AND_Gate and_2, 5 bits wide
  Multiplexer #(.select(4), .width(5)) multiplexer_5 (
    .in1({5{1'b0}}), .in2(subtractor_1_out), .in4(adder_1_out), .in8(Parallel_Count), .in10(undriven),
    .in11(undriven), .out(Count_Output), .sel({Parallel_Loading, Shift_In, Shift_Out__Input, Parallel_Unload}));  // open: in0, in3, in5, in6, in7, in9, in12, in13, in14, in15, en
  Multiplexer #(.select(3)) multiplexer_6 (
    .in0(Parallel_Output[20]), .in1(Parallel_Input[20]), .in2(Parallel_Output[19]), .in3(Parallel_Input[20]),
    .in4(multiplexer_4_out), .in5(Parallel_Input[20]), .in7(Parallel_Input[20]), .out(multiplexer_6_out),
    .sel({Shift_In, Shift_Out__Input, Parallel_Loading}));  // open: in6, en
  D_Flip_Flop d_ff_2 (.clk(CLK), .D(multiplexer_6_out), .Q(Parallel_Output[20]));  // open: Qn, preset, en, reset
  Multiplexer #(.select(5)) multiplexer_7 (
    .in0(Parallel_Output[19]), .in31(Serial_Input), .out(multiplexer_7_out), .sel(and_3_out));  // open: in1, in2, in3, in4, in5, in6, in7, in8, in9, in10, in11, in12, in13, in14, in15, in16, in17, in18, in19, in20, in21, in22, in23, in24, in25, in26, in27, in28, in29, in30, en
  assign and_3_out = Count & 5'b00010;  // AND_Gate and_3, 5 bits wide
  Multiplexer #(.select(3)) multiplexer_8 (
    .in0(Parallel_Output[19]), .in1(Parallel_Input[19]), .in2(Parallel_Output[18]), .in3(Parallel_Input[19]),
    .in4(multiplexer_7_out), .in5(Parallel_Input[19]), .in7(Parallel_Input[19]), .out(multiplexer_8_out),
    .sel({Shift_In, Shift_Out__Input, Parallel_Loading}));  // open: in6, en
  D_Flip_Flop d_ff_3 (.clk(CLK), .D(multiplexer_8_out), .Q(Parallel_Output[19]));  // open: Qn, preset, en, reset
  Multiplexer #(.select(5)) multiplexer_9 (
    .in0(Parallel_Output[18]), .in31(Serial_Input), .out(multiplexer_9_out), .sel(and_4_out));  // open: in1, in2, in3, in4, in5, in6, in7, in8, in9, in10, in11, in12, in13, in14, in15, in16, in17, in18, in19, in20, in21, in22, in23, in24, in25, in26, in27, in28, in29, in30, en
  assign and_4_out = Count & 5'b00011;  // AND_Gate and_4, 5 bits wide
  Multiplexer #(.select(3)) multiplexer_10 (
    .in0(Parallel_Output[18]), .in1(Parallel_Input[18]), .in2(Parallel_Output[17]), .in3(Parallel_Input[18]),
    .in4(multiplexer_9_out), .in5(Parallel_Input[18]), .in7(Parallel_Input[18]), .out(multiplexer_10_out),
    .sel({Shift_In, Shift_Out__Input, Parallel_Loading}));  // open: in6, en
  D_Flip_Flop d_ff_4 (.clk(CLK), .D(multiplexer_10_out), .Q(Parallel_Output[18]));  // open: Qn, preset, en, reset
  Multiplexer #(.select(5)) multiplexer_11 (
    .in0(Parallel_Output[17]), .in31(Serial_Input), .out(multiplexer_11_out), .sel(and_5_out));  // open: in1, in2, in3, in4, in5, in6, in7, in8, in9, in10, in11, in12, in13, in14, in15, in16, in17, in18, in19, in20, in21, in22, in23, in24, in25, in26, in27, in28, in29, in30, en
  assign and_5_out = Count & 5'b00100;  // AND_Gate and_5, 5 bits wide
  Multiplexer #(.select(3)) multiplexer_12 (
    .in0(Parallel_Output[17]), .in1(Parallel_Input[17]), .in2(Parallel_Output[16]), .in3(Parallel_Input[17]),
    .in4(multiplexer_11_out), .in5(Parallel_Input[17]), .in7(Parallel_Input[17]), .out(multiplexer_12_out),
    .sel({Shift_In, Shift_Out__Input, Parallel_Loading}));  // open: in6, en
  D_Flip_Flop d_ff_5 (.clk(CLK), .D(multiplexer_12_out), .Q(Parallel_Output[17]));  // open: Qn, preset, en, reset
  Multiplexer #(.select(5)) multiplexer_13 (
    .in0(Parallel_Output[16]), .in31(Serial_Input), .out(multiplexer_13_out), .sel(and_6_out));  // open: in1, in2, in3, in4, in5, in6, in7, in8, in9, in10, in11, in12, in13, in14, in15, in16, in17, in18, in19, in20, in21, in22, in23, in24, in25, in26, in27, in28, in29, in30, en
  assign and_6_out = Count & 5'b00101;  // AND_Gate and_6, 5 bits wide
  Multiplexer #(.select(3)) multiplexer_14 (
    .in0(Parallel_Output[16]), .in1(Parallel_Input[16]), .in2(Parallel_Output[15]), .in3(Parallel_Input[16]),
    .in4(multiplexer_13_out), .in5(Parallel_Input[16]), .in7(Parallel_Input[16]), .out(multiplexer_14_out),
    .sel({Shift_In, Shift_Out__Input, Parallel_Loading}));  // open: in6, en
  D_Flip_Flop d_ff_6 (.clk(CLK), .D(multiplexer_14_out), .Q(Parallel_Output[16]));  // open: Qn, preset, en, reset
  Multiplexer #(.select(5)) multiplexer_15 (
    .in0(Parallel_Output[15]), .in31(Serial_Input), .out(multiplexer_15_out), .sel(and_7_out));  // open: in1, in2, in3, in4, in5, in6, in7, in8, in9, in10, in11, in12, in13, in14, in15, in16, in17, in18, in19, in20, in21, in22, in23, in24, in25, in26, in27, in28, in29, in30, en
  assign and_7_out = Count & 5'b00110;  // AND_Gate and_7, 5 bits wide
  Multiplexer #(.select(3)) multiplexer_16 (
    .in0(Parallel_Output[15]), .in1(Parallel_Input[15]), .in2(Parallel_Output[14]), .in3(Parallel_Input[15]),
    .in4(multiplexer_15_out), .in5(Parallel_Input[15]), .in7(Parallel_Input[15]), .out(multiplexer_16_out),
    .sel({Shift_In, Shift_Out__Input, Parallel_Loading}));  // open: in6, en
  D_Flip_Flop d_ff_7 (.clk(CLK), .D(multiplexer_16_out), .Q(Parallel_Output[15]));  // open: Qn, preset, en, reset
  Multiplexer #(.select(5)) multiplexer_17 (
    .in0(Parallel_Output[14]), .in31(Serial_Input), .out(multiplexer_17_out), .sel(and_8_out));  // open: in1, in2, in3, in4, in5, in6, in7, in8, in9, in10, in11, in12, in13, in14, in15, in16, in17, in18, in19, in20, in21, in22, in23, in24, in25, in26, in27, in28, in29, in30, en
  assign and_8_out = Count & 5'b00111;  // AND_Gate and_8, 5 bits wide
  Multiplexer #(.select(3)) multiplexer_18 (
    .in0(Parallel_Output[14]), .in1(Parallel_Input[14]), .in2(Parallel_Output[13]), .in3(Parallel_Input[14]),
    .in4(multiplexer_17_out), .in5(Parallel_Input[14]), .in7(Parallel_Input[14]), .out(multiplexer_18_out),
    .sel({Shift_In, Shift_Out__Input, Parallel_Loading}));  // open: in6, en
  D_Flip_Flop d_ff_8 (.clk(CLK), .D(multiplexer_18_out), .Q(Parallel_Output[14]));  // open: Qn, preset, en, reset
  Multiplexer #(.select(5)) multiplexer_19 (
    .in0(Parallel_Output[13]), .in31(Serial_Input), .out(multiplexer_19_out), .sel(and_9_out));  // open: in1, in2, in3, in4, in5, in6, in7, in8, in9, in10, in11, in12, in13, in14, in15, in16, in17, in18, in19, in20, in21, in22, in23, in24, in25, in26, in27, in28, in29, in30, en
  assign and_9_out = Count & 5'b01000;  // AND_Gate and_9, 5 bits wide
  Multiplexer #(.select(3)) multiplexer_20 (
    .in0(Parallel_Output[13]), .in1(Parallel_Input[13]), .in2(Parallel_Output[12]), .in3(Parallel_Input[13]),
    .in4(multiplexer_19_out), .in5(Parallel_Input[13]), .in7(Parallel_Input[13]), .out(multiplexer_20_out),
    .sel({Shift_In, Shift_Out__Input, Parallel_Loading}));  // open: in6, en
  D_Flip_Flop d_ff_9 (.clk(CLK), .D(multiplexer_20_out), .Q(Parallel_Output[13]));  // open: Qn, preset, en, reset
  Multiplexer #(.select(5)) multiplexer_21 (
    .in0(Parallel_Output[12]), .in31(Serial_Input), .out(multiplexer_21_out), .sel(and_10_out));  // open: in1, in2, in3, in4, in5, in6, in7, in8, in9, in10, in11, in12, in13, in14, in15, in16, in17, in18, in19, in20, in21, in22, in23, in24, in25, in26, in27, in28, in29, in30, en
  assign and_10_out = Count & 5'b01001;  // AND_Gate and_10, 5 bits wide
  Multiplexer #(.select(3)) multiplexer_22 (
    .in0(Parallel_Output[12]), .in1(Parallel_Input[12]), .in2(Parallel_Output[11]), .in3(Parallel_Input[12]),
    .in4(multiplexer_21_out), .in5(Parallel_Input[12]), .in7(Parallel_Input[12]), .out(multiplexer_22_out),
    .sel({Shift_In, Shift_Out__Input, Parallel_Loading}));  // open: in6, en
  D_Flip_Flop d_ff_10 (.clk(CLK), .D(multiplexer_22_out), .Q(Parallel_Output[12]));  // open: Qn, preset, en, reset
  Multiplexer #(.select(5)) multiplexer_23 (
    .in0(Parallel_Output[11]), .in31(Serial_Input), .out(multiplexer_23_out), .sel(and_11_out));  // open: in1, in2, in3, in4, in5, in6, in7, in8, in9, in10, in11, in12, in13, in14, in15, in16, in17, in18, in19, in20, in21, in22, in23, in24, in25, in26, in27, in28, in29, in30, en
  assign and_11_out = Count & 5'b01010;  // AND_Gate and_11, 5 bits wide
  Multiplexer #(.select(3)) multiplexer_24 (
    .in0(Parallel_Output[11]), .in1(Parallel_Input[11]), .in2(Parallel_Output[10]), .in3(Parallel_Input[11]),
    .in4(multiplexer_23_out), .in5(Parallel_Input[11]), .in7(Parallel_Input[11]), .out(multiplexer_24_out),
    .sel({Shift_In, Shift_Out__Input, Parallel_Loading}));  // open: in6, en
  D_Flip_Flop d_ff_11 (.clk(CLK), .D(multiplexer_24_out), .Q(Parallel_Output[11]));  // open: Qn, preset, en, reset
  Multiplexer #(.select(5)) multiplexer_25 (
    .in0(Parallel_Output[10]), .in31(Serial_Input), .out(multiplexer_25_out), .sel(and_12_out));  // open: in1, in2, in3, in4, in5, in6, in7, in8, in9, in10, in11, in12, in13, in14, in15, in16, in17, in18, in19, in20, in21, in22, in23, in24, in25, in26, in27, in28, in29, in30, en
  assign and_12_out = Count & 5'b01011;  // AND_Gate and_12, 5 bits wide
  Multiplexer #(.select(3)) multiplexer_26 (
    .in0(Parallel_Output[10]), .in1(Parallel_Input[10]), .in2(Parallel_Output[9]), .in3(Parallel_Input[10]),
    .in4(multiplexer_25_out), .in5(Parallel_Input[10]), .in7(Parallel_Input[10]), .out(multiplexer_26_out),
    .sel({Shift_In, Shift_Out__Input, Parallel_Loading}));  // open: in6, en
  D_Flip_Flop d_ff_12 (.clk(CLK), .D(multiplexer_26_out), .Q(Parallel_Output[10]));  // open: Qn, preset, en, reset
  Multiplexer #(.select(5)) multiplexer_27 (
    .in0(Parallel_Output[9]), .in31(Serial_Input), .out(multiplexer_27_out), .sel(and_13_out));  // open: in1, in2, in3, in4, in5, in6, in7, in8, in9, in10, in11, in12, in13, in14, in15, in16, in17, in18, in19, in20, in21, in22, in23, in24, in25, in26, in27, in28, in29, in30, en
  assign and_13_out = Count & 5'b01100;  // AND_Gate and_13, 5 bits wide
  Multiplexer #(.select(3)) multiplexer_28 (
    .in0(Parallel_Output[9]), .in1(Parallel_Input[9]), .in2(Parallel_Output[8]), .in3(Parallel_Input[9]),
    .in4(multiplexer_27_out), .in5(Parallel_Input[9]), .in7(Parallel_Input[9]), .out(multiplexer_28_out),
    .sel({Shift_In, Shift_Out__Input, Parallel_Loading}));  // open: in6, en
  D_Flip_Flop d_ff_13 (.clk(CLK), .D(multiplexer_28_out), .Q(Parallel_Output[9]));  // open: Qn, preset, en, reset
  Multiplexer #(.select(5)) multiplexer_29 (
    .in0(Parallel_Output[8]), .in31(Serial_Input), .out(multiplexer_29_out), .sel(and_14_out));  // open: in1, in2, in3, in4, in5, in6, in7, in8, in9, in10, in11, in12, in13, in14, in15, in16, in17, in18, in19, in20, in21, in22, in23, in24, in25, in26, in27, in28, in29, in30, en
  assign and_14_out = Count & 5'b01101;  // AND_Gate and_14, 5 bits wide
  Multiplexer #(.select(3)) multiplexer_30 (
    .in0(Parallel_Output[8]), .in1(Parallel_Input[8]), .in2(Parallel_Output[7]), .in3(Parallel_Input[8]),
    .in4(multiplexer_29_out), .in5(Parallel_Input[8]), .in7(Parallel_Input[8]), .out(multiplexer_30_out),
    .sel({Shift_In, Shift_Out__Input, Parallel_Loading}));  // open: in6, en
  D_Flip_Flop d_ff_14 (.clk(CLK), .D(multiplexer_30_out), .Q(Parallel_Output[8]));  // open: Qn, preset, en, reset
  Multiplexer #(.select(5)) multiplexer_31 (
    .in0(Parallel_Output[7]), .in31(Serial_Input), .out(multiplexer_31_out), .sel(and_15_out));  // open: in1, in2, in3, in4, in5, in6, in7, in8, in9, in10, in11, in12, in13, in14, in15, in16, in17, in18, in19, in20, in21, in22, in23, in24, in25, in26, in27, in28, in29, in30, en
  assign and_15_out = Count & 5'b01110;  // AND_Gate and_15, 5 bits wide
  Multiplexer #(.select(3)) multiplexer_32 (
    .in0(Parallel_Output[7]), .in1(Parallel_Input[7]), .in2(Parallel_Output[6]), .in3(Parallel_Input[7]),
    .in4(multiplexer_31_out), .in5(Parallel_Input[7]), .in7(Parallel_Input[7]), .out(multiplexer_32_out),
    .sel({Shift_In, Shift_Out__Input, Parallel_Loading}));  // open: in6, en
  D_Flip_Flop d_ff_15 (.clk(CLK), .D(multiplexer_32_out), .Q(Parallel_Output[7]));  // open: Qn, preset, en, reset
  Multiplexer #(.select(5)) multiplexer_33 (
    .in0(Parallel_Output[6]), .in31(Serial_Input), .out(multiplexer_33_out), .sel(and_16_out));  // open: in1, in2, in3, in4, in5, in6, in7, in8, in9, in10, in11, in12, in13, in14, in15, in16, in17, in18, in19, in20, in21, in22, in23, in24, in25, in26, in27, in28, in29, in30, en
  assign and_16_out = Count & 5'b01111;  // AND_Gate and_16, 5 bits wide
  Multiplexer #(.select(3)) multiplexer_34 (
    .in0(Parallel_Output[6]), .in1(Parallel_Input[6]), .in2(Parallel_Output[5]), .in3(Parallel_Input[6]),
    .in4(multiplexer_33_out), .in5(Parallel_Input[6]), .in7(Parallel_Input[6]), .out(multiplexer_34_out),
    .sel({Shift_In, Shift_Out__Input, Parallel_Loading}));  // open: in6, en
  D_Flip_Flop d_ff_16 (.clk(CLK), .D(multiplexer_34_out), .Q(Parallel_Output[6]));  // open: Qn, preset, en, reset
  Multiplexer #(.select(5)) multiplexer_35 (
    .in0(Parallel_Output[5]), .in31(Serial_Input), .out(multiplexer_35_out), .sel(and_17_out));  // open: in1, in2, in3, in4, in5, in6, in7, in8, in9, in10, in11, in12, in13, in14, in15, in16, in17, in18, in19, in20, in21, in22, in23, in24, in25, in26, in27, in28, in29, in30, en
  assign and_17_out = Count & 5'b10000;  // AND_Gate and_17, 5 bits wide
  Multiplexer #(.select(3)) multiplexer_36 (
    .in0(Parallel_Output[5]), .in1(Parallel_Input[5]), .in2(Parallel_Output[4]), .in3(Parallel_Input[5]),
    .in4(multiplexer_35_out), .in5(Parallel_Input[5]), .in7(Parallel_Input[5]), .out(multiplexer_36_out),
    .sel({Shift_In, Shift_Out__Input, Parallel_Loading}));  // open: in6, en
  D_Flip_Flop d_ff_17 (.clk(CLK), .D(multiplexer_36_out), .Q(Parallel_Output[5]));  // open: Qn, preset, en, reset
  Multiplexer #(.select(5)) multiplexer_37 (
    .in0(Parallel_Output[4]), .in31(Serial_Input), .out(multiplexer_37_out), .sel(and_18_out));  // open: in1, in2, in3, in4, in5, in6, in7, in8, in9, in10, in11, in12, in13, in14, in15, in16, in17, in18, in19, in20, in21, in22, in23, in24, in25, in26, in27, in28, in29, in30, en
  assign and_18_out = Count & 5'b10001;  // AND_Gate and_18, 5 bits wide
  Multiplexer #(.select(3)) multiplexer_38 (
    .in0(Parallel_Output[4]), .in1(Parallel_Input[4]), .in2(Parallel_Output[3]), .in3(Parallel_Input[4]),
    .in4(multiplexer_37_out), .in5(Parallel_Input[4]), .in7(Parallel_Input[4]), .out(multiplexer_38_out),
    .sel({Shift_In, Shift_Out__Input, Parallel_Loading}));  // open: in6, en
  D_Flip_Flop d_ff_18 (.clk(CLK), .D(multiplexer_38_out), .Q(Parallel_Output[4]));  // open: Qn, preset, en, reset
  Multiplexer #(.select(5)) multiplexer_39 (
    .in0(Parallel_Output[3]), .in31(Serial_Input), .out(multiplexer_39_out), .sel(and_19_out));  // open: in1, in2, in3, in4, in5, in6, in7, in8, in9, in10, in11, in12, in13, in14, in15, in16, in17, in18, in19, in20, in21, in22, in23, in24, in25, in26, in27, in28, in29, in30, en
  assign and_19_out = Count & 5'b10010;  // AND_Gate and_19, 5 bits wide
  Multiplexer #(.select(3)) multiplexer_40 (
    .in0(Parallel_Output[3]), .in1(Parallel_Input[3]), .in2(Parallel_Output[2]), .in3(Parallel_Input[3]),
    .in4(multiplexer_39_out), .in5(Parallel_Input[3]), .in7(Parallel_Input[3]), .out(multiplexer_40_out),
    .sel({Shift_In, Shift_Out__Input, Parallel_Loading}));  // open: in6, en
  D_Flip_Flop d_ff_19 (.clk(CLK), .D(multiplexer_40_out), .Q(Parallel_Output[3]));  // open: Qn, preset, en, reset
  Multiplexer #(.select(5)) multiplexer_41 (
    .in0(Parallel_Output[2]), .in31(Serial_Input), .out(multiplexer_41_out), .sel(and_20_out));  // open: in1, in2, in3, in4, in5, in6, in7, in8, in9, in10, in11, in12, in13, in14, in15, in16, in17, in18, in19, in20, in21, in22, in23, in24, in25, in26, in27, in28, in29, in30, en
  assign and_20_out = Count & 5'b10011;  // AND_Gate and_20, 5 bits wide
  Multiplexer #(.select(3)) multiplexer_42 (
    .in0(Parallel_Output[2]), .in1(Parallel_Input[2]), .in2(Parallel_Output[1]), .in3(Parallel_Input[2]),
    .in4(multiplexer_41_out), .in5(Parallel_Input[2]), .in7(Parallel_Input[2]), .out(multiplexer_42_out),
    .sel({Shift_In, Shift_Out__Input, Parallel_Loading}));  // open: in6, en
  D_Flip_Flop d_ff_20 (.clk(CLK), .D(multiplexer_42_out), .Q(Parallel_Output[2]));  // open: Qn, preset, en, reset
  Multiplexer #(.select(5)) multiplexer_43 (
    .in0(Parallel_Output[1]), .in31(Serial_Input), .out(multiplexer_43_out), .sel(and_21_out));  // open: in1, in2, in3, in4, in5, in6, in7, in8, in9, in10, in11, in12, in13, in14, in15, in16, in17, in18, in19, in20, in21, in22, in23, in24, in25, in26, in27, in28, in29, in30, en
  assign and_21_out = Count & 5'b10100;  // AND_Gate and_21, 5 bits wide
  Multiplexer #(.select(3)) multiplexer_44 (
    .in0(Parallel_Output[1]), .in1(Parallel_Input[1]), .in2(Parallel_Output[0]), .in3(Parallel_Input[1]),
    .in4(multiplexer_43_out), .in5(Parallel_Input[1]), .in7(Parallel_Input[1]), .out(multiplexer_44_out),
    .sel({Shift_In, Shift_Out__Input, Parallel_Loading}));  // open: in6, en
  D_Flip_Flop d_ff_21 (.clk(CLK), .D(multiplexer_44_out), .Q(Parallel_Output[1]));  // open: Qn, preset, en, reset
  Multiplexer #(.select(5)) multiplexer_45 (
    .in0(Parallel_Output[0]), .in31(Serial_Input), .out(multiplexer_45_out), .sel(and_22_out));  // open: in1, in2, in3, in4, in5, in6, in7, in8, in9, in10, in11, in12, in13, in14, in15, in16, in17, in18, in19, in20, in21, in22, in23, in24, in25, in26, in27, in28, in29, in30, en
  assign and_22_out = Count & 5'b10101;  // AND_Gate and_22, 5 bits wide
  Multiplexer #(.select(3)) multiplexer_46 (
    .in0(Parallel_Output[0]), .in1(Parallel_Input[0]), .in3(Parallel_Input[0]), .in4(multiplexer_45_out),
    .in5(Parallel_Input[0]), .in7(Parallel_Input[0]), .out(multiplexer_46_out),
    .sel({Shift_In, Shift_Out__Input, Parallel_Loading}));  // open: in2, in6, en
  D_Flip_Flop d_ff_22 (.clk(CLK), .D(multiplexer_46_out), .Q(Parallel_Output[0]));  // open: Qn, preset, en, reset

  // Other names for the same wires on the sheet: PU = Parallel_Unload; PL = Parallel_Loading; SHO = Shift_Out__Input;
  //   SHI = Shift_In; PC[4:0] = Parallel_Count; PI[21:0] = Parallel_Input; PI22 = Parallel_Input[0];
  //   PI21 = Parallel_Input[1]; PI20 = Parallel_Input[2]; PI19 = Parallel_Input[3]; PI18 = Parallel_Input[4];
  //   PI17 = Parallel_Input[5]; PI16 = Parallel_Input[6]; PI15 = Parallel_Input[7]; PI14 = Parallel_Input[8];
  //   PI13 = Parallel_Input[9]; PI12 = Parallel_Input[10]; PI11 = Parallel_Input[11]; PI10 = Parallel_Input[12];
  //   PI9 = Parallel_Input[13]; PI8 = Parallel_Input[14]; PI7 = Parallel_Input[15]; PI6 = Parallel_Input[16];
  //   PI5 = Parallel_Input[17]; PI4 = Parallel_Input[18]; PI3 = Parallel_Input[19]; PI2 = Parallel_Input[20];
  //   PI1 = Parallel_Input[21]; D22 = Parallel_Output[0]; PO[21:0] = Parallel_Output; PO22 = Parallel_Output[0];
  //   D21 = Parallel_Output[1]; PO21 = Parallel_Output[1]; D20 = Parallel_Output[2]; PO20 = Parallel_Output[2];
  //   D19 = Parallel_Output[3]; PO19 = Parallel_Output[3]; D18 = Parallel_Output[4]; PO18 = Parallel_Output[4];
  //   D17 = Parallel_Output[5]; PO17 = Parallel_Output[5]; D16 = Parallel_Output[6]; PO16 = Parallel_Output[6];
  //   D15 = Parallel_Output[7]; PO15 = Parallel_Output[7]; D14 = Parallel_Output[8]; PO14 = Parallel_Output[8];
  //   D13 = Parallel_Output[9]; PO13 = Parallel_Output[9]; D12 = Parallel_Output[10]; PO12 = Parallel_Output[10];
  //   D11 = Parallel_Output[11]; PO11 = Parallel_Output[11]; D10 = Parallel_Output[12]; PO10 = Parallel_Output[12];
  //   D9 = Parallel_Output[13]; PO9 = Parallel_Output[13]; D8 = Parallel_Output[14]; PO8 = Parallel_Output[14];
  //   D7 = Parallel_Output[15]; PO7 = Parallel_Output[15]; D6 = Parallel_Output[16]; PO6 = Parallel_Output[16];
  //   D5 = Parallel_Output[17]; PO5 = Parallel_Output[17]; D4 = Parallel_Output[18]; PO4 = Parallel_Output[18];
  //   D3 = Parallel_Output[19]; PO3 = Parallel_Output[19]; D2 = Parallel_Output[20]; PO2 = Parallel_Output[20];
  //   D1 = Parallel_Output[21]; PO1 = Parallel_Output[21]; SI = Serial_Input; SO = Serial_Output

  // Notes on the sheet:
  //   Can both be 1, parallel takes precedence 
  //   Push?
  //   Enable
  //   Enable
  //   How many bits we are about to parallel load
  //   Enable? Pop?
  //   Set Count to 0
  //   Take all bits and unload simultaneously
endmodule

module Bit_stuffer (
  input  Divisor,
  input  ISDATA,
  input  WW,
  input  CLK,
  input  [21:0] DATAIN,
  output TXI,
  output CW,
  output TX
);

  wire and_1_out, and_2_out, and_3_out, multiplexer_1_out, nor_1_out, undriven, undriven_2;
  wire [2:0] _1_Counter_q;

  FIFO fifo_1 (
    .CLK(CLK), .Serial_Input(ISDATA), .Serial_Output(undriven));  // open: Count_Output, Shift_In, Parallel_Loading, Parallel_Count, Parallel_Input, Shift_Out__Input, Count, Parallel_Unload, Parallel_Output
  FIFO fifo_2 (
    .CLK(CLK), .Parallel_Input(DATAIN), .Serial_Output(undriven_2));  // open: Count_Output, Serial_Input, Shift_In, Parallel_Loading, Parallel_Count, Shift_Out__Input, Count, Parallel_Unload, Parallel_Output
  Multiplexer multiplexer_1 (.in0(1'b0), .in1(1'b1), .out(multiplexer_1_out), .en(and_3_out));  // open: sel
  Counter #(.width(3), .max('h7)) _1_Counter (.Q(_1_Counter_q));  // open: load, D, count, carry, clk, clr
  Multiplexer multiplexer_2 (.in0(undriven_2), .in1(multiplexer_1_out), .out(TX), .sel(and_3_out));  // open: en
  and and_1 (and_1_out, 1'b1, _1_Counter_q[0]);
  nor nor_1 (nor_1_out, _1_Counter_q[1], 1'b0);
  and and_2 (and_2_out, _1_Counter_q[2], 1'b1);
  and and_3 (and_3_out, and_1_out, and_2_out);

  // Notes on the sheet:
  //   Finished a word
endmodule
